// Logisim project logism_circuit.circ as structural Verilog
module top (
  input  [15:0] man_pc,
  input  clock,
  input  man_pc_sel,
  input  reset,
  input  [15:0] write_addr,
  input  instruction_write,
  input  [31:0] write_data,
  output [4:0] out_8,
  output [4:0] out_9,
  output [15:0] out_10,
  output [4:0] out_11,
  output [4:0] out_12,
  output out_13,
  output out_14,
  output out_15,
  output out_16,
  output out_17,
  output [15:0] out_18,
  output [15:0] out_19,
  output [15:0] out_20,
  output [15:0] out_21,
  output [15:0] out_22,
  output [15:0] out_23,
  output [15:0] out_24,
  output [15:0] out_25
);

  wire alu_1_eq, alu_1_gt, alu_1_lt, cache_control_1_hit, cache_control_1_miss, control_1_cache_read,
       control_1_cache_write, control_1_instr_fetch, control_1_mem_fifo_push, control_1_memory_enable,
       control_1_mreg_en, control_1_push_reg_fifo, control_1_read_hit, control_1_read_miss, control_1_reg_en,
       control_1_write_miss, dec_1_set, decode_unit_1_unset, memory_buffer_1_empty, memory_buffer_1_full,
       rat_control_1_pause, rat_control_1_rh_delay, rat_control_1_rm_delay, rat_control_1_wm_delay,
       rs_read_register_1_out_7, rs_read_register_1_out_8, rs_read_register_1_out_9,
       rs_read_register_1_out_10, rs_read_register_1_out_11, rs_read_register_1_out_12,
       rs_read_register_1_out_13, rs_read_register_2_out_7, rs_read_register_2_out_8,
       rs_read_register_2_out_9, rs_read_register_2_out_10, rs_read_register_2_out_11,
       rs_read_register_2_out_12, rs_read_register_2_out_13, rs_write_reg_1_out_8, rs_write_reg_1_out_9,
       rs_write_reg_1_out_10, rs_write_reg_1_out_11, rs_write_reg_1_out_12, rs_write_reg_1_out_13,
       rs_write_reg_1_out_14;
  wire [1:0] stat_add_1_out1, stat_add_1_out2, stat_add_1_out3, stat_add_1_out4, stat_add_1_out5,
       stat_add_1_out6, stat_add_1_out7;
  wire [2:0] control_1_alu_op, control_1_mreg_sel, control_1_rd_out, control_1_reg_sel, control_1_rega_sel,
       control_1_regb_sel, control_1_rs1_out, control_1_rs2_out, dec_1_rd, dec_1_rs1, dec_1_rs2,
       decode_unit_1_funct3, memory_buffer_1_data_out_2, multiplexer_1_out, multiplexer_2_out,
       rat_control_1_free_addr, rat_read_1_rd_count, rat_write_1_rs1_count, rat_write_1_rs2_count,
       rs1_fifo_1_reg_out, rs1_fifo_2_reg_out, rs1_fifo_3_reg_out, rs_counter_1_reg_out;
  wire [3:0] adder_2_out, adder_3_out;
  wire [4:0] adder_1_out, cache_control_1_miss_addr_5, cache_control_1_set_addr_5, control_1_cache_addr_out,
       register_1_q;
  wire [6:0] decode_unit_1_funct7, decode_unit_1_opcode;
  wire [7:0] rat_control_1_instr_buffer_stat_reg;
  wire [11:0] decode_unit_1_imm_11_0;
  wire [15:0] alu_1_alu_out, cache_1_data_out, cache_control_1_miss_addr_16, control_1_alua, control_1_alub,
       control_1_cache_data, control_1_m_fifo_data, control_1_memory_address, control_1_memory_data,
       control_1_register_data, data_memory_1_data_out, memory_buffer_1_data_out, pc_buffer_1_pc_out,
       registers_1_rega_out, registers_1_regb_out, registers_1_regc_out;
  wire [22:0] control_1_mem_fifo_data;
  wire [22:19] memory_buffer_1_data_out_3;
  wire [31:0] instruction_buffer_1_instruction_out, prog_mem_1_ram_data_out;

  Adder #(.width(5)) adder_1 (.a(register_1_q), .b(5'b00001), .out(adder_1_out));  // open: cin, cout
  Register #(.width(5)) register_1 (.D(adder_1_out), .clk(clock), .Q(register_1_q), .clr(reset));  // open: en
  Subtractor #(.width(5)) subtractor_1 (.a(register_1_q), .b(5'b00010), .out(out_8));  // open: bin, bout
  pc_buffer pc_buffer_1 (
    .pc_in(out_10), .addr_in(rat_control_1_free_addr), .enable(control_1_instr_fetch), .clock(clock),
    .reset(reset), .addr_out(rs_counter_1_reg_out), .pc_out(pc_buffer_1_pc_out));
  instruction_buffer instruction_buffer_1 (
    .instruction_in(prog_mem_1_ram_data_out), .addr_in(rat_control_1_free_addr),
    .enable(control_1_instr_fetch), .clock(clock), .reset(reset), .addr_out(rs_counter_1_reg_out),
    .instruction_out(instruction_buffer_1_instruction_out));
  prog_mem prog_mem_1 (
    .load_addr(out_10), .write_addr(write_addr), .we(instruction_write), .clock(clock), .in_data(write_data),
    .ram_data_out(prog_mem_1_ram_data_out));
  RS_read_register rs_read_register_1 (
    .rs(dec_1_rs1), .addr(rat_control_1_free_addr), .en(control_1_instr_fetch),
    .rd_check(rs1_fifo_3_reg_out), .reset(reset), .clock(clock), .out_7(rs_read_register_1_out_7),
    .out_8(rs_read_register_1_out_8), .out_9(rs_read_register_1_out_9), .out_10(rs_read_register_1_out_10),
    .out_11(rs_read_register_1_out_11), .out_12(rs_read_register_1_out_12), .out_13(rs_read_register_1_out_13));
  RS_read_register rs_read_register_2 (
    .rs(dec_1_rs2), .addr(rat_control_1_free_addr), .en(control_1_instr_fetch),
    .rd_check(rs1_fifo_3_reg_out), .reset(reset), .clock(clock), .out_7(rs_read_register_2_out_7),
    .out_8(rs_read_register_2_out_8), .out_9(rs_read_register_2_out_9), .out_10(rs_read_register_2_out_10),
    .out_11(rs_read_register_2_out_11), .out_12(rs_read_register_2_out_12), .out_13(rs_read_register_2_out_13));
  RS_write_reg rs_write_reg_1 (
    .rd(dec_1_rd), .addr(rat_control_1_free_addr), .en(control_1_instr_fetch),
    .rs1_check(rs1_fifo_1_reg_out), .rs2_check(rs1_fifo_2_reg_out), .reset(reset), .clock(clock),
    .out_8(rs_write_reg_1_out_8), .out_9(rs_write_reg_1_out_9), .out_10(rs_write_reg_1_out_10),
    .out_11(rs_write_reg_1_out_11), .out_12(rs_write_reg_1_out_12), .out_13(rs_write_reg_1_out_13),
    .out_14(rs_write_reg_1_out_14));
  dec dec_1 (
    .instruction(prog_mem_1_ram_data_out), .rs1(dec_1_rs1), .rs2(dec_1_rs2), .rd(dec_1_rd), .r_type(out_13),
    .i_type(out_14), .s_type(out_15), .b_type(out_16), .j_type(out_17), .set(dec_1_set));
  stat_add stat_add_1 (
    .in1a(rs_read_register_1_out_7), .in1b(rs_read_register_2_out_7), .in1c(rs_write_reg_1_out_8),
    .in2a(rs_read_register_1_out_8), .in2b(rs_read_register_2_out_8), .in2c(rs_write_reg_1_out_9),
    .in3a(rs_read_register_1_out_9), .in3b(rs_read_register_2_out_9), .in3c(rs_write_reg_1_out_10),
    .in4a(rs_read_register_1_out_10), .in4b(rs_read_register_2_out_10), .in4c(rs_write_reg_1_out_11),
    .in5a(rs_read_register_1_out_11), .in5b(rs_read_register_2_out_11), .in5c(rs_write_reg_1_out_12),
    .in6a(rs_read_register_1_out_12), .in6b(rs_read_register_2_out_12), .in6c(rs_write_reg_1_out_13),
    .in7a(rs_read_register_1_out_13), .in7b(rs_read_register_2_out_13), .in7c(rs_write_reg_1_out_14),
    .out1(stat_add_1_out1), .out2(stat_add_1_out2), .out3(stat_add_1_out3), .out4(stat_add_1_out4),
    .out5(stat_add_1_out5), .out6(stat_add_1_out6), .out7(stat_add_1_out7));
  RAT_read rat_read_1 (
    .rs1(dec_1_rs1), .rs2(dec_1_rs2), .rd(dec_1_rd), .rs1_check(rs1_fifo_1_reg_out),
    .rs2_check(rs1_fifo_2_reg_out), .enable(control_1_instr_fetch), .reset(reset), .clock(clock),
    .rd_count(rat_read_1_rd_count));
  RAT_write rat_write_1 (
    .rd(dec_1_rd), .rs1(dec_1_rs1), .rs2(dec_1_rs2), .rd_check(rs1_fifo_3_reg_out),
    .enable(control_1_instr_fetch), .reset(reset), .clock(clock), .rs1_count(rat_write_1_rs1_count),
    .rs2_count(rat_write_1_rs2_count));
  Adder #(.width(4)) adder_2 (
    .a({1'b0, rat_read_1_rd_count}), .b({1'b0, rat_write_1_rs1_count}), .out(adder_2_out));  // open: cin, cout
  Adder #(.width(4)) adder_3 (
    .a(adder_2_out), .b({1'b0, rat_write_1_rs2_count}), .out(adder_3_out));  // open: cin, cout
  RS_counter rs_counter_1 (
    .sum(adder_3_out), .addr(rat_control_1_free_addr), .enable(control_1_instr_fetch), .m1(stat_add_1_out1),
    .m2(stat_add_1_out2), .m3(stat_add_1_out3), .m4(stat_add_1_out4), .m5(stat_add_1_out5),
    .m6(stat_add_1_out6), .m7(stat_add_1_out7), .reg_status_bit(rat_control_1_instr_buffer_stat_reg),
    .reset(reset), .clock(clock), .reg_out(rs_counter_1_reg_out));
  decode_unit decode_unit_1 (
    .instruction(instruction_buffer_1_instruction_out), .opcode(decode_unit_1_opcode), .rd(out_9),
    .funct3(decode_unit_1_funct3), .rs1(out_11), .rs2(out_12), .funct7(decode_unit_1_funct7),
    .imm_11_0(decode_unit_1_imm_11_0), .unset(decode_unit_1_unset));  // open: r_type, i_type, s_type, b_type, j_type
  RAT_control rat_control_1 (
    .read_miss(control_1_read_miss), .write_miss(control_1_write_miss), .read_hit(control_1_read_hit),
    .unset(decode_unit_1_unset), .set(dec_1_set), .addr_used(rat_control_1_free_addr),
    .enable(control_1_instr_fetch), .addr_unused(rs_counter_1_reg_out), .reset(reset), .clock(clock),
    .rm_delay(rat_control_1_rm_delay), .wm_delay(rat_control_1_wm_delay), .rh_delay(rat_control_1_rh_delay),
    .pause(rat_control_1_pause), .instr_buffer_stat_reg(rat_control_1_instr_buffer_stat_reg),
    .free_addr(rat_control_1_free_addr));
  alu alu_1 (
    .regA(control_1_alua), .regB(control_1_alub), .operand(control_1_alu_op), .alu_out(alu_1_alu_out),
    .gt(alu_1_gt), .eq(alu_1_eq), .lt(alu_1_lt));
  data_memory data_memory_1 (
    .addr(control_1_memory_address), .we(control_1_memory_enable), .clock(clock),
    .datain(control_1_memory_data), .data_out(data_memory_1_data_out));
  registers registers_1 (
    .reg_in(control_1_register_data), .mem_in(control_1_m_fifo_data), .en_reg(control_1_reg_en),
    .en_mem(control_1_mreg_en), .reg_addr(control_1_reg_sel), .mem_addr(control_1_mreg_sel),
    .regA_sel(control_1_rega_sel), .regB_sel(control_1_regb_sel), .regC_sel(memory_buffer_1_data_out_2),
    .reset(reset), .clock(clock), .regA_out(registers_1_rega_out), .regB_out(registers_1_regb_out),
    .regC_out(registers_1_regc_out), .reg0(out_18), .reg1(out_19), .reg2(out_20), .reg3(out_21),
    .reg4(out_22), .reg5(out_23), .reg6(out_24), .reg7(out_25));
  control control_1 (
    .opcode(decode_unit_1_opcode), .lru_addr_5(cache_control_1_miss_addr_5),
    .cache_set_addr_5(cache_control_1_set_addr_5), .rh_delay(rat_control_1_rh_delay),
    .wm_delay(rat_control_1_wm_delay), .cache_set_addr_16(memory_buffer_1_data_out),
    .lru_address_16(cache_control_1_miss_addr_16), .memory_out(data_memory_1_data_out),
    .regC_data(registers_1_regc_out), .rm_delay(rat_control_1_rm_delay), .miss(cache_control_1_miss),
    .mem_fifo_empty(memory_buffer_1_empty), .hit(cache_control_1_hit),
    .read_write(memory_buffer_1_data_out_3[19]), .cache_data_out(cache_1_data_out),
    .mem_fifo_set_addr(memory_buffer_1_data_out_2), .mem_fifo_full(memory_buffer_1_full), .rs1(out_11),
    .funct3(decode_unit_1_funct3), .funct7(decode_unit_1_funct7), .rd(out_9), .regA(registers_1_rega_out),
    .imm_11_0(decode_unit_1_imm_11_0), .regB(registers_1_regb_out), .alu_out(alu_1_alu_out), .rs2(out_12),
    .pause(rat_control_1_pause), .instr_stat_reg(rat_control_1_instr_buffer_stat_reg), .manual_pc(man_pc),
    .man_sel(man_pc_sel), .cur_pc(pc_buffer_1_pc_out), .eq(alu_1_eq), .gt(alu_1_gt), .lt(alu_1_lt),
    .clock(clock), .reset(reset), .reg_en(control_1_reg_en), .push_reg_fifo(control_1_push_reg_fifo),
    .cache_addr_out(control_1_cache_addr_out), .mreg_en(control_1_mreg_en),
    .memory_enable(control_1_memory_enable), .memory_address(control_1_memory_address),
    .cache_data(control_1_cache_data), .read_miss(control_1_read_miss), .write_miss(control_1_write_miss),
    .cache_write(control_1_cache_write), .read_hit(control_1_read_hit), .cache_read(control_1_cache_read),
    .m_fifo_data(control_1_m_fifo_data), .memory_data(control_1_memory_data), .mreg_sel(control_1_mreg_sel),
    .mem_fifo_push(control_1_mem_fifo_push), .rs1_out(control_1_rs1_out), .rs2_out(control_1_rs2_out),
    .rd_out(control_1_rd_out), .regA_sel(control_1_rega_sel), .mem_fifo_data(control_1_mem_fifo_data),
    .alu_op(control_1_alu_op), .reg_sel(control_1_reg_sel), .aluA(control_1_alua), .aluB(control_1_alub),
    .register_data(control_1_register_data), .regB_sel(control_1_regb_sel),
    .instr_fetch(control_1_instr_fetch), .program_counter(out_10));  // open: branch, jump, memory, write_hit
  Multiplexer #(.width(3), .enable("false")) multiplexer_1 (
    .in0(3'b000), .in1(memory_buffer_1_data_out_2), .out(multiplexer_1_out),
    .sel(memory_buffer_1_data_out_3[19]));
  Multiplexer #(.width(3), .enable("false")) multiplexer_2 (
    .in0(memory_buffer_1_data_out_2), .in1(3'b000), .out(multiplexer_2_out),
    .sel(memory_buffer_1_data_out_3[19]));
  memory_buffer memory_buffer_1 (
    .data_in(control_1_mem_fifo_data), .push(control_1_mem_fifo_push), .pop(control_1_cache_read),
    .reset(reset), .clock(clock),
    .data_out({memory_buffer_1_data_out_3, memory_buffer_1_data_out_2, memory_buffer_1_data_out}),
    .full(memory_buffer_1_full), .empty(memory_buffer_1_empty));
  cache cache_1 (
    .addr(control_1_cache_addr_out), .we(control_1_cache_write), .clock(clock),
    .data_in(control_1_cache_data), .data_out(cache_1_data_out));
  cache_control cache_control_1 (
    .set_addr_16(memory_buffer_1_data_out), .cache_access(control_1_cache_read), .reset(reset),
    .clock(clock), .miss_addr_5(cache_control_1_miss_addr_5), .set_addr_5(cache_control_1_set_addr_5),
    .miss_addr_16(cache_control_1_miss_addr_16), .hit(cache_control_1_hit), .miss(cache_control_1_miss));
  rs1_fifo rs1_fifo_1 (
    .reg_in(control_1_rs1_out), .mem_in(memory_buffer_1_data_out_3[22:20]), .push_mem(control_1_cache_read),
    .push_reg(control_1_push_reg_fifo), .reset(reset), .clock(clock), .reg_out(rs1_fifo_1_reg_out));
  rs1_fifo rs1_fifo_2 (
    .reg_in(control_1_rs2_out), .mem_in(multiplexer_1_out), .push_mem(control_1_cache_read),
    .push_reg(control_1_push_reg_fifo), .reset(reset), .clock(clock), .reg_out(rs1_fifo_2_reg_out));
  rs1_fifo rs1_fifo_3 (
    .reg_in(control_1_rd_out), .mem_in(multiplexer_2_out), .push_mem(control_1_cache_read),
    .push_reg(control_1_push_reg_fifo), .reset(reset), .clock(clock), .reg_out(rs1_fifo_3_reg_out));
endmodule

module decode_unit (
  input  [31:0] instruction,
  output [6:0] opcode,
  output r_type,
  output [4:0] rd,
  output [2:0] funct3,
  output i_type,
  output [4:0] rs1,
  output s_type,
  output [4:0] rs2,
  output [6:0] funct7,
  output b_type,
  output j_type,
  output [11:0] imm_11_0,
  output unset
);

  wire and_1_out, and_2_out, or_1_out, or_2_out;

  and and_1 (and_1_out, instruction[12], s_type);
  and and_2 (and_2_out, ~instruction[12], s_type);  // AND_Gate
  or or_1 (or_1_out, r_type, and_1_out, b_type);
  Comparator #(.width(7), .mode("unsigned")) comparator_1 (
    .a(instruction[6:0]), .b(7'b0110011), .eq(r_type));  // open: gt, lt
  Comparator #(.width(7), .mode("unsigned")) comparator_2 (
    .a(instruction[6:0]), .b(7'b0010011), .eq(i_type));  // open: gt, lt
  Comparator #(.width(7), .mode("unsigned")) comparator_3 (
    .a(instruction[6:0]), .b(7'b0100011), .eq(s_type));  // open: gt, lt
  Comparator #(.width(7), .mode("unsigned")) comparator_4 (
    .a(instruction[6:0]), .b(7'b1100011), .eq(b_type));  // open: gt, lt
  Comparator #(.width(7), .mode("unsigned")) comparator_5 (
    .a(instruction[6:0]), .b(7'b1100111), .eq(j_type));  // open: gt, lt
  Multiplexer #(.width(5), .enable("false")) multiplexer_1 (
    .in0({5{1'b0}}), .in1(instruction[24:20]), .out(rs2), .sel(or_1_out));
  Multiplexer #(.width(5), .enable("false")) multiplexer_2 (
    .in0({5{1'b0}}), .in1(instruction[11:7]), .out(rd), .sel(or_2_out));
  or or_2 (or_2_out, and_2_out, r_type, j_type, i_type);
  or or_3 (unset, j_type, b_type);

  assign funct3 = instruction[14:12];
  assign funct7 = instruction[31:25];
  assign imm_11_0 = instruction[31:20];
  assign opcode = instruction[6:0];
  assign rs1 = instruction[19:15];
endmodule

module pc_buffer (
  input  [15:0] pc_in,
  input  [2:0] addr_in,
  input  enable,
  input  clock,
  input  reset,
  input  [2:0] addr_out,
  output [15:0] pc_out
);

  wire and_1_out, and_2_out, and_3_out, and_4_out, and_5_out, and_6_out, and_7_out, and_8_out,
       comparator_1_eq, comparator_2_eq, comparator_3_eq, comparator_4_eq, comparator_5_eq, comparator_6_eq,
       comparator_7_eq, comparator_8_eq;
  wire [15:0] register_1_q, register_2_q, register_3_q, register_4_q, register_5_q, register_6_q,
       register_7_q, register_8_q, register_9_q;

  Comparator #(.width(3), .mode("unsigned")) comparator_1 (
    .a(3'b000), .b(addr_in), .eq(comparator_1_eq));  // open: gt, lt
  Comparator #(.width(3), .mode("unsigned")) comparator_2 (
    .a(3'b001), .b(addr_in), .eq(comparator_2_eq));  // open: gt, lt
  Comparator #(.width(3), .mode("unsigned")) comparator_3 (
    .a(3'b010), .b(addr_in), .eq(comparator_3_eq));  // open: gt, lt
  Comparator #(.width(3), .mode("unsigned")) comparator_4 (
    .a(3'b011), .b(addr_in), .eq(comparator_4_eq));  // open: gt, lt
  Comparator #(.width(3), .mode("unsigned")) comparator_5 (
    .a(3'b100), .b(addr_in), .eq(comparator_5_eq));  // open: gt, lt
  Comparator #(.width(3), .mode("unsigned")) comparator_6 (
    .a(3'b101), .b(addr_in), .eq(comparator_6_eq));  // open: gt, lt
  Comparator #(.width(3), .mode("unsigned")) comparator_7 (
    .a(3'b110), .b(addr_in), .eq(comparator_7_eq));  // open: gt, lt
  Comparator #(.width(3), .mode("unsigned")) comparator_8 (
    .a(3'b111), .b(addr_in), .eq(comparator_8_eq));  // open: gt, lt
  Register #(.width(16)) register_1 (.D(pc_in), .clk(clock), .Q(register_1_q), .clr(reset));  // open: en
  Register #(.width(16)) register_2 (.D(register_1_q), .en(and_1_out), .clk(clock), .Q(register_2_q), .clr(reset));
  and and_1 (and_1_out, comparator_1_eq, enable);
  Register #(.width(16)) register_3 (.D(register_1_q), .en(and_2_out), .clk(clock), .Q(register_3_q), .clr(reset));
  and and_2 (and_2_out, comparator_2_eq, enable);
  Register #(.width(16)) register_4 (.D(register_1_q), .en(and_3_out), .clk(clock), .Q(register_4_q), .clr(reset));
  and and_3 (and_3_out, comparator_3_eq, enable);
  Register #(.width(16)) register_5 (.D(register_1_q), .en(and_4_out), .clk(clock), .Q(register_5_q), .clr(reset));
  and and_4 (and_4_out, comparator_4_eq, enable);
  Register #(.width(16)) register_6 (.D(register_1_q), .en(and_5_out), .clk(clock), .Q(register_6_q), .clr(reset));
  and and_5 (and_5_out, comparator_5_eq, enable);
  Register #(.width(16)) register_7 (.D(register_1_q), .en(and_6_out), .clk(clock), .Q(register_7_q), .clr(reset));
  and and_6 (and_6_out, comparator_6_eq, enable);
  Register #(.width(16)) register_8 (.D(register_1_q), .en(and_7_out), .clk(clock), .Q(register_8_q), .clr(reset));
  and and_7 (and_7_out, comparator_7_eq, enable);
  Register #(.width(16)) register_9 (.D(register_1_q), .en(and_8_out), .clk(clock), .Q(register_9_q), .clr(reset));
  and and_8 (and_8_out, comparator_8_eq, enable);
  Multiplexer #(.select(3), .width(16), .enable("false")) multiplexer_1 (
    .in0(register_2_q), .in1(register_3_q), .in2(register_4_q), .in3(register_5_q), .in4(register_6_q),
    .in5(register_7_q), .in6(register_8_q), .in7(register_9_q), .out(pc_out), .sel(addr_out));
endmodule

module instruction_buffer (
  input  [31:0] instruction_in,
  input  [2:0] addr_in,
  input  enable,
  input  clock,
  input  reset,
  input  [2:0] addr_out,
  output [31:0] instruction_out
);

  wire and_1_out, and_2_out, and_3_out, and_4_out, and_5_out, and_6_out, and_7_out, and_8_out,
       comparator_1_eq, comparator_2_eq, comparator_3_eq, comparator_4_eq, comparator_5_eq, comparator_6_eq,
       comparator_7_eq, comparator_8_eq;
  wire [31:0] register_1_q, register_2_q, register_3_q, register_4_q, register_5_q, register_6_q,
       register_7_q, register_8_q;

  Comparator #(.width(3), .mode("unsigned")) comparator_1 (
    .a(3'b000), .b(addr_in), .eq(comparator_1_eq));  // open: gt, lt
  Comparator #(.width(3), .mode("unsigned")) comparator_2 (
    .a(3'b001), .b(addr_in), .eq(comparator_2_eq));  // open: gt, lt
  Comparator #(.width(3), .mode("unsigned")) comparator_3 (
    .a(3'b010), .b(addr_in), .eq(comparator_3_eq));  // open: gt, lt
  Comparator #(.width(3), .mode("unsigned")) comparator_4 (
    .a(3'b011), .b(addr_in), .eq(comparator_4_eq));  // open: gt, lt
  Comparator #(.width(3), .mode("unsigned")) comparator_5 (
    .a(3'b100), .b(addr_in), .eq(comparator_5_eq));  // open: gt, lt
  Comparator #(.width(3), .mode("unsigned")) comparator_6 (
    .a(3'b101), .b(addr_in), .eq(comparator_6_eq));  // open: gt, lt
  Comparator #(.width(3), .mode("unsigned")) comparator_7 (
    .a(3'b110), .b(addr_in), .eq(comparator_7_eq));  // open: gt, lt
  Comparator #(.width(3), .mode("unsigned")) comparator_8 (
    .a(3'b111), .b(addr_in), .eq(comparator_8_eq));  // open: gt, lt
  Register #(.width(32)) register_1 (.D(instruction_in), .en(and_1_out), .clk(clock), .Q(register_1_q), .clr(reset));
  and and_1 (and_1_out, comparator_1_eq, enable);
  Register #(.width(32)) register_2 (.D(instruction_in), .en(and_2_out), .clk(clock), .Q(register_2_q), .clr(reset));
  and and_2 (and_2_out, comparator_2_eq, enable);
  Register #(.width(32)) register_3 (.D(instruction_in), .en(and_3_out), .clk(clock), .Q(register_3_q), .clr(reset));
  and and_3 (and_3_out, comparator_3_eq, enable);
  Register #(.width(32)) register_4 (.D(instruction_in), .en(and_4_out), .clk(clock), .Q(register_4_q), .clr(reset));
  and and_4 (and_4_out, comparator_4_eq, enable);
  Register #(.width(32)) register_5 (.D(instruction_in), .en(and_5_out), .clk(clock), .Q(register_5_q), .clr(reset));
  and and_5 (and_5_out, comparator_5_eq, enable);
  Register #(.width(32)) register_6 (.D(instruction_in), .en(and_6_out), .clk(clock), .Q(register_6_q), .clr(reset));
  and and_6 (and_6_out, comparator_6_eq, enable);
  Register #(.width(32)) register_7 (.D(instruction_in), .en(and_7_out), .clk(clock), .Q(register_7_q), .clr(reset));
  and and_7 (and_7_out, comparator_7_eq, enable);
  Register #(.width(32)) register_8 (.D(instruction_in), .en(and_8_out), .clk(clock), .Q(register_8_q), .clr(reset));
  and and_8 (and_8_out, comparator_8_eq, enable);
  Multiplexer #(.select(3), .width(32), .enable("false")) multiplexer_1 (
    .in0(register_1_q), .in1(register_2_q), .in2(register_3_q), .in3(register_4_q), .in4(register_5_q),
    .in5(register_6_q), .in6(register_7_q), .in7(register_8_q), .out(instruction_out), .sel(addr_out));
endmodule

module prog_mem (
  input  [15:0] load_addr,
  input  [15:0] write_addr,
  input  we,
  input  clock,
  input  [31:0] in_data,
  output [31:0] ram_data_out
);

  wire [15:0] multiplexer_1_out;

  Multiplexer #(.width(16), .enable("false")) multiplexer_1 (
    .in0(load_addr), .in1(write_addr), .out(multiplexer_1_out), .sel(we));
  RAM #(.addrWidth(16), .dataWidth(32), .databus("bibus")) ram_1 (
    .addr(multiplexer_1_out), .we(we), .clk(clock), .din(in_data), .dout(ram_data_out));  // open: oe
endmodule

module stat_add (
  input  in1a,
  input  in1b,
  input  in1c,
  input  in2a,
  input  in2b,
  input  in2c,
  input  in3a,
  input  in3b,
  input  in3c,
  input  in4a,
  input  in4b,
  input  in4c,
  input  in5a,
  input  in5b,
  input  in5c,
  input  in6a,
  input  in6b,
  input  in6c,
  input  in7a,
  input  in7b,
  input  in7c,
  output [1:0] out1,
  output [1:0] out2,
  output [1:0] out3,
  output [1:0] out4,
  output [1:0] out5,
  output [1:0] out6,
  output [1:0] out7
);

  wire [1:0] adder_1_out, adder_2_out, adder_3_out, adder_4_out, adder_5_out, adder_6_out, adder_7_out;

  Adder #(.width(2)) adder_1 (.a({in1a, 1'b0}), .b({in1b, 1'b0}), .out(adder_1_out));  // open: cin, cout
  Adder #(.width(2)) adder_2 (.a({in2a, 1'b0}), .b({in2b, 1'b0}), .out(adder_2_out));  // open: cin, cout
  Adder #(.width(2)) adder_3 (.a({in3a, 1'b0}), .b({in3b, 1'b0}), .out(adder_3_out));  // open: cin, cout
  Adder #(.width(2)) adder_4 (.a({in4a, 1'b0}), .b({in4b, 1'b0}), .out(adder_4_out));  // open: cin, cout
  Adder #(.width(2)) adder_5 (.a({in5a, 1'b0}), .b({in5b, 1'b0}), .out(adder_5_out));  // open: cin, cout
  Adder #(.width(2)) adder_6 (.a({in6a, 1'b0}), .b({in6b, 1'b0}), .out(adder_6_out));  // open: cin, cout
  Adder #(.width(2)) adder_7 (.a({in7a, 1'b0}), .b({in7b, 1'b0}), .out(adder_7_out));  // open: cin, cout
  Adder #(.width(2)) adder_8 (.a(adder_1_out), .b({in1c, 1'b0}), .out(out1));  // open: cin, cout
  Adder #(.width(2)) adder_9 (.a(adder_2_out), .b({in2c, 1'b0}), .out(out2));  // open: cin, cout
  Adder #(.width(2)) adder_10 (.a(adder_3_out), .b({in3c, 1'b0}), .out(out3));  // open: cin, cout
  Adder #(.width(2)) adder_11 (.a(adder_4_out), .b({in4c, 1'b0}), .out(out4));  // open: cin, cout
  Adder #(.width(2)) adder_12 (.a(adder_5_out), .b({in5c, 1'b0}), .out(out5));  // open: cin, cout
  Adder #(.width(2)) adder_13 (.a(adder_6_out), .b({in6c, 1'b0}), .out(out6));  // open: cin, cout
  Adder #(.width(2)) adder_14 (.a(adder_7_out), .b({in7c, 1'b0}), .out(out7));  // open: cin, cout
endmodule

module control (
  input  [6:0] opcode,
  input  [4:0] lru_addr_5,
  input  [4:0] cache_set_addr_5,
  input  rh_delay,
  input  wm_delay,
  input  [15:0] cache_set_addr_16,
  input  [15:0] lru_address_16,
  input  [15:0] memory_out,
  input  [15:0] regC_data,
  input  rm_delay,
  input  miss,
  input  mem_fifo_empty,
  input  hit,
  input  read_write,
  input  [15:0] cache_data_out,
  input  [2:0] mem_fifo_set_addr,
  input  mem_fifo_full,
  input  [4:0] rs1,
  input  [2:0] funct3,
  input  [6:0] funct7,
  input  [4:0] rd,
  input  [15:0] regA,
  input  [11:0] imm_11_0,
  input  [15:0] regB,
  input  [15:0] alu_out,
  input  [4:0] rs2,
  input  pause,
  input  [7:0] instr_stat_reg,
  input  [15:0] manual_pc,
  input  man_sel,
  input  [15:0] cur_pc,
  input  eq,
  input  gt,
  input  lt,
  input  clock,
  input  reset,
  output reg_en,
  output push_reg_fifo,
  output branch,
  output jump,
  output memory,
  output [4:0] cache_addr_out,
  output mreg_en,
  output memory_enable,
  output [15:0] memory_address,
  output [15:0] cache_data,
  output read_miss,
  output write_miss,
  output cache_write,
  output write_hit,
  output read_hit,
  output cache_read,
  output [15:0] m_fifo_data,
  output [15:0] memory_data,
  output [2:0] mreg_sel,
  output mem_fifo_push,
  output [2:0] rs1_out,
  output [2:0] rs2_out,
  output [2:0] rd_out,
  output [2:0] regA_sel,
  output [22:0] mem_fifo_data,
  output [2:0] alu_op,
  output [2:0] reg_sel,
  output [15:0] aluA,
  output [15:0] aluB,
  output [15:0] register_data,
  output [2:0] regB_sel,
  output instr_fetch,
  output [15:0] program_counter
);

  wire and_1_out, and_2_out, and_5_out, and_6_out, and_7_out, and_8_out, and_12_out, and_13_out,
       comparator_2_eq, comparator_3_eq, comparator_4_eq, comparator_8_eq, comparator_9_eq,
       multiplexer_17_out, not_1_out, not_2_out, not_3_out, or_1_out, or_2_out, or_3_out, or_4_out, or_5_out,
       or_6_out, or_7_out, or_8_out, or_9_out, or_10_out, or_11_out, or_13_out, or_14_out;
  wire [4:0] multiplexer_3_out;
  wire [15:0] adder_1_out, adder_2_out, adder_3_out, adder_4_out, adder_6_out, multiplexer_1_out,
       multiplexer_2_out, multiplexer_4_out, multiplexer_5_out, multiplexer_11_out, multiplexer_14_out,
       multiplexer_15_out, multiplexer_16_out, multiplexer_21_out, multiplexer_27_out, multiplexer_29_out;

  Comparator #(.mode("unsigned")) comparator_1 (.a(instr_stat_reg), .b({8{1'b1}}), .lt(instr_fetch));  // open: gt, eq
  Adder #(.width(16)) adder_1 (.a(program_counter), .b(16'h1), .out(adder_1_out));  // open: cin, cout
  Multiplexer #(.width(16), .enable("false")) multiplexer_1 (
    .in0({16{1'b0}}), .in1({4'b0000, imm_11_0}), .out(multiplexer_1_out), .sel(comparator_4_eq));
  Adder #(.width(16)) adder_2 (.a(program_counter), .b(16'h1), .out(adder_2_out));  // open: cin, cout
  Multiplexer #(.width(16), .enable("false")) multiplexer_2 (
    .in0(multiplexer_14_out), .in1(program_counter), .out(multiplexer_2_out), .sel(pause));
  Adder #(.width(16)) adder_3 (.a(regA), .b({4'b0000, funct7, rs2}), .out(adder_3_out));  // open: cin, cout
  Adder #(.width(16)) adder_4 (.a(cur_pc), .b(regA), .out(adder_4_out));  // open: cin, cout
  Comparator #(.width(3), .mode("unsigned")) comparator_2 (
    .a(funct3), .b(3'b001), .eq(comparator_2_eq));  // open: gt, lt
  not not_1 (not_1_out, eq);
  not not_2 (not_2_out, gt);
  not not_3 (not_3_out, lt);
  Comparator #(.width(7), .mode("unsigned")) comparator_3 (
    .a(opcode), .b(7'b0110011), .eq(comparator_3_eq));  // open: gt, lt
  Comparator #(.width(7), .mode("unsigned")) comparator_4 (
    .a(opcode), .b(7'b0010011), .eq(comparator_4_eq));  // open: gt, lt
  Comparator #(.width(7), .mode("unsigned")) comparator_5 (.a(opcode), .b(7'b1100011), .eq(branch));  // open: gt, lt
  Comparator #(.width(7), .mode("unsigned")) comparator_6 (.a(opcode), .b(7'b1101111), .eq(jump));  // open: gt, lt
  Comparator #(.width(7), .mode("unsigned")) comparator_7 (.a(opcode), .b(7'b0100011), .eq(memory));  // open: gt, lt
  Multiplexer #(.width(5), .enable("false")) multiplexer_3 (
    .in0({5{1'b0}}), .in1(lru_addr_5), .out(multiplexer_3_out), .sel(or_1_out));
  or or_1 (or_1_out, and_2_out, and_8_out);
  and and_1 (and_1_out, wm_delay, write_miss);
  and and_2 (and_2_out, write_miss, ~wm_delay);  // AND_Gate
  Multiplexer #(.width(16), .enable("false")) multiplexer_4 (
    .in0({16{1'b0}}), .in1(cache_set_addr_16), .out(multiplexer_4_out), .sel(and_8_out));
  or or_2 (or_2_out, and_1_out, and_7_out);
  Multiplexer #(.width(16), .enable("false")) multiplexer_5 (
    .in0({16{1'b0}}), .in1(memory_out), .out(multiplexer_5_out), .sel(and_7_out));
  or or_3 (or_3_out, and_1_out, write_hit);
  and and_3 (read_miss, ~read_write, and_5_out);  // AND_Gate
  and and_4 (write_miss, read_write, and_5_out);
  and and_5 (and_5_out, ~mem_fifo_empty, miss);  // AND_Gate
  and and_6 (and_6_out, ~mem_fifo_empty, hit);  // AND_Gate
  Multiplexer #(.width(3), .enable("false")) multiplexer_6 (
    .in0(3'b000), .in1(mem_fifo_set_addr), .out(mreg_sel), .sel(or_4_out));
  or or_4 (or_4_out, and_7_out, rh_delay);
  Adder #(.width(16)) adder_5 (.a({{9{1'b0}}, funct7}), .b(regA), .out(mem_fifo_data[15:0]));  // open: cin, cout
  Multiplexer #(.width(3), .enable("false")) multiplexer_7 (
    .in0(rd[2:0]), .in1(rs2[2:0]), .out(mem_fifo_data[18:16]), .sel(funct3[0]));
  Multiplexer #(.width(3), .enable("false")) multiplexer_8 (.in0(3'b000), .in1(rd[2:0]), .out(reg_sel), .sel(or_5_out));
  or or_5 (or_5_out, jump, comparator_4_eq, comparator_3_eq);
  Multiplexer #(.width(16), .enable("false")) multiplexer_9 (.in0({16{1'b0}}), .in1(regA), .out(aluA), .sel(or_6_out));
  or or_6 (or_6_out, branch, comparator_4_eq, comparator_3_eq);
  Multiplexer #(.width(16), .enable("false")) multiplexer_10 (
    .in0(multiplexer_1_out), .in1(regB), .out(aluB), .sel(or_7_out));
  or or_7 (or_7_out, branch, comparator_3_eq);
  Multiplexer #(.width(16), .enable("false")) multiplexer_11 (
    .in0({16{1'b0}}), .in1(adder_1_out), .out(multiplexer_11_out), .sel(jump));
  Multiplexer #(.width(16), .enable("false")) multiplexer_12 (
    .in0(multiplexer_11_out), .in1(alu_out), .out(register_data), .sel(or_8_out));
  or or_8 (or_8_out, comparator_3_eq, comparator_4_eq);
  Multiplexer #(.width(3), .enable("false")) multiplexer_13 (
    .in0(3'b000), .in1(rs2[2:0]), .out(regB_sel), .sel(or_9_out));
  or or_9 (or_9_out, comparator_3_eq, branch);
  Multiplexer #(.width(16), .enable("false")) multiplexer_14 (
    .in0(program_counter), .in1(adder_2_out), .out(multiplexer_14_out), .sel(instr_fetch));
  Multiplexer #(.width(16), .enable("false")) multiplexer_15 (
    .in0(multiplexer_2_out), .in1(manual_pc), .out(multiplexer_15_out), .sel(man_sel));
  Multiplexer #(.width(16), .enable("false")) multiplexer_16 (
    .in0(adder_3_out), .in1(adder_4_out), .out(multiplexer_16_out), .sel(comparator_2_eq));
  Adder #(.width(16)) adder_6 (.a(cur_pc), .b({{9{1'b0}}, funct7}), .out(adder_6_out));  // open: cin, cout
  Multiplexer #(.select(3), .enable("false")) multiplexer_17 (
    .in0(eq), .in1(not_1_out), .in2(gt), .in3(not_2_out), .in4(lt), .in5(not_3_out), .in6(1'b0), .in7(1'b0),
    .out(multiplexer_17_out), .sel(funct3));
  or or_10 (or_10_out, comparator_3_eq, comparator_4_eq, jump);
  Multiplexer #(.width(5), .enable("false")) multiplexer_18 (
    .in0(multiplexer_3_out), .in1(cache_set_addr_5), .out(cache_addr_out), .sel(or_11_out));
  or or_11 (or_11_out, write_hit, read_hit, and_7_out, and_1_out);
  or or_12 (memory_enable, and_1_out, and_7_out);
  Multiplexer #(.width(16), .enable("false")) multiplexer_19 (
    .in0(multiplexer_4_out), .in1(lru_address_16), .out(memory_address), .sel(or_2_out));
  Multiplexer #(.width(16), .enable("false")) multiplexer_20 (
    .in0(multiplexer_5_out), .in1(regC_data), .out(cache_data), .sel(or_3_out));
  and and_7 (and_7_out, rm_delay, read_miss);
  and and_8 (and_8_out, read_miss, ~rm_delay);  // AND_Gate
  and and_9 (write_hit, and_6_out, read_write);
  and and_10 (read_hit, and_6_out, ~read_write);  // AND_Gate
  Multiplexer #(.width(16), .enable("false")) multiplexer_21 (
    .in0({16{1'b0}}), .in1(memory_out), .out(multiplexer_21_out), .sel(and_7_out));
  Multiplexer #(.width(16), .enable("false")) multiplexer_22 (
    .in0(multiplexer_21_out), .in1(cache_data_out), .out(m_fifo_data), .sel(rh_delay));
  Multiplexer #(.width(16), .enable("false")) multiplexer_23 (
    .in0({16{1'b0}}), .in1(cache_data_out), .out(memory_data), .sel(or_13_out));
  or or_13 (or_13_out, and_1_out, and_7_out);
  and and_11 (mem_fifo_push, memory, ~mem_fifo_full);  // AND_Gate
  Multiplexer #(.width(3), .enable("false")) multiplexer_24 (
    .in0(3'b000), .in1(rs1[2:0]), .out(rs1_out), .sel(or_14_out));
  Multiplexer #(.width(3), .enable("false")) multiplexer_25 (
    .in0(3'b000), .in1(rs2[2:0]), .out(rs2_out), .sel(or_14_out));
  Multiplexer #(.width(3), .enable("false")) multiplexer_26 (
    .in0(3'b000), .in1(rd[2:0]), .out(rd_out), .sel(or_14_out));
  Comparator #(.width(3), .mode("unsigned")) comparator_8 (
    .a(funct3), .b(3'b000), .eq(comparator_8_eq));  // open: gt, lt
  Comparator #(.width(7), .mode("unsigned")) comparator_9 (
    .a(funct7), .b(7'b0100000), .eq(comparator_9_eq));  // open: gt, lt
  Multiplexer #(.width(16), .enable("false")) multiplexer_27 (
    .in0(multiplexer_15_out), .in1(multiplexer_16_out), .out(multiplexer_27_out), .sel(jump));
  and and_12 (and_12_out, multiplexer_17_out, branch);
  or or_14 (or_14_out, comparator_3_eq, comparator_4_eq, branch, jump);
  or or_15 (cache_write, and_1_out, and_7_out, write_hit);
  Multiplexer #(.width(3), .enable("false")) multiplexer_28 (
    .in0(funct3), .in1(3'b011), .out(alu_op), .sel(and_13_out));
  and and_13 (and_13_out, comparator_8_eq, comparator_9_eq);
  Multiplexer #(.width(16), .enable("false")) multiplexer_29 (
    .in0(multiplexer_27_out), .in1(adder_6_out), .out(multiplexer_29_out), .sel(and_12_out));
  or or_16 (mreg_en, rh_delay, and_7_out);
  or or_17 (cache_read, cache_write, rh_delay);
  Register #(.width(1)) register_1 (.D(or_10_out), .clk(clock), .Q(reg_en), .clr(reset));  // open: en
  Register #(.width(1)) register_2 (.D(or_14_out), .clk(clock), .Q(push_reg_fifo), .clr(reset));  // open: en
  Register #(.width(16)) register_3 (
    .D(multiplexer_29_out), .clk(clock), .Q(program_counter), .clr(reset));  // open: en

  assign mem_fifo_data[22:19] = {rs1[2:0], funct3[0]};
  assign regA_sel = rs1[2:0];
endmodule

module dec (
  input  [31:0] instruction,
  output [2:0] rs1,
  output [2:0] rs2,
  output [2:0] rd,
  output r_type,
  output i_type,
  output s_type,
  output b_type,
  output j_type,
  output set
);

  wire and_1_out, and_2_out, or_1_out, or_2_out;
  wire [4:3] multiplexer_1_out, multiplexer_2_out;

  Comparator #(.width(7), .mode("unsigned")) comparator_1 (
    .a(instruction[6:0]), .b(7'b0110011), .eq(r_type));  // open: gt, lt
  Comparator #(.width(7), .mode("unsigned")) comparator_2 (
    .a(instruction[6:0]), .b(7'b0010011), .eq(i_type));  // open: gt, lt
  Comparator #(.width(7), .mode("unsigned")) comparator_3 (
    .a(instruction[6:0]), .b(7'b0100011), .eq(s_type));  // open: gt, lt
  Comparator #(.width(7), .mode("unsigned")) comparator_4 (
    .a(instruction[6:0]), .b(7'b1100011), .eq(b_type));  // open: gt, lt
  Comparator #(.width(7), .mode("unsigned")) comparator_5 (
    .a(instruction[6:0]), .b(7'b1100111), .eq(j_type));  // open: gt, lt
  and and_1 (and_1_out, instruction[12], s_type);
  and and_2 (and_2_out, ~instruction[12], s_type);  // AND_Gate
  Multiplexer #(.width(5), .enable("false")) multiplexer_1 (
    .in0({5{1'b0}}), .in1(instruction[24:20]), .out({multiplexer_1_out, rs2}), .sel(or_1_out));
  or or_1 (or_1_out, r_type, and_1_out, b_type);
  Multiplexer #(.width(5), .enable("false")) multiplexer_2 (
    .in0({5{1'b0}}), .in1(instruction[11:7]), .out({multiplexer_2_out, rd}), .sel(or_2_out));
  or or_2 (or_2_out, and_2_out, r_type, i_type, j_type);
  or or_3 (set, j_type, b_type);

  assign rs1 = instruction[17:15];
endmodule

module alu (
  input  [15:0] regA,
  input  [15:0] regB,
  input  [2:0] operand,
  output [15:0] alu_out,
  output gt,
  output eq,
  output lt
);

  wire comparator_1_lt;
  wire [15:0] adder_1_out, and_1_out, multiplexer_1_out, or_1_out, shifter_1_out, shifter_2_out,
       subtractor_1_out, xor_1_out;

  Adder #(.width(16)) adder_1 (.a(regA), .b(regB), .out(adder_1_out));  // open: cin, cout
  Shifter #(.width(16)) shifter_1 (.in(regA), .\dist (regB[3:0]), .out(shifter_1_out));
  Multiplexer #(.width(16), .enable("false")) multiplexer_1 (
    .in0({16{1'b0}}), .in1(16'h1), .out(multiplexer_1_out), .sel(comparator_1_lt));
  Comparator #(.width(16)) comparator_1 (.a(regA), .b(regB), .lt(comparator_1_lt));  // open: gt, eq
  Subtractor #(.width(16)) subtractor_1 (.a(regA), .b(regB), .out(subtractor_1_out));  // open: bin, bout
  assign xor_1_out = regA ^ regB;  // XOR_Gate xor_1, 16 bits wide
  Shifter #(.width(16), .shift("lr")) shifter_2 (.in(regA), .\dist (regB[3:0]), .out(shifter_2_out));
  assign or_1_out = regA | regB;  // OR_Gate or_1, 16 bits wide
  assign and_1_out = regA & regB;  // AND_Gate and_1, 16 bits wide
  Comparator #(.width(16)) comparator_2 (.a(regA), .b(regB), .gt(gt), .eq(eq), .lt(lt));
  Multiplexer #(.select(3), .width(16), .enable("false")) multiplexer_2 (
    .in0(adder_1_out), .in1(shifter_1_out), .in2(multiplexer_1_out), .in3(subtractor_1_out), .in4(xor_1_out),
    .in5(shifter_2_out), .in6(or_1_out), .in7(and_1_out), .out(alu_out), .sel(operand));
endmodule

module registers (
  input  [15:0] reg_in,
  input  [15:0] mem_in,
  input  en_reg,
  input  en_mem,
  input  [2:0] reg_addr,
  input  [2:0] mem_addr,
  input  [2:0] regA_sel,
  input  [2:0] regB_sel,
  input  [2:0] regC_sel,
  input  reset,
  input  clock,
  output [15:0] regA_out,
  output [15:0] regB_out,
  output [15:0] regC_out,
  output [15:0] reg0,
  output [15:0] reg1,
  output [15:0] reg2,
  output [15:0] reg3,
  output [15:0] reg4,
  output [15:0] reg5,
  output [15:0] reg6,
  output [15:0] reg7
);

  wire and_1_out, and_2_out, and_3_out, and_4_out, and_5_out, and_6_out, and_7_out, and_8_out, and_9_out,
       and_10_out, and_11_out, and_12_out, and_13_out, and_14_out, and_15_out, and_16_out, comparator_1_eq,
       comparator_2_eq, comparator_3_eq, comparator_4_eq, comparator_5_eq, comparator_6_eq, comparator_7_eq,
       comparator_8_eq, comparator_9_eq, comparator_10_eq, comparator_11_eq, comparator_12_eq,
       comparator_13_eq, comparator_14_eq, comparator_15_eq, comparator_16_eq;
  wire [15:0] multiplexer_1_out, multiplexer_2_out, multiplexer_3_out, multiplexer_4_out, multiplexer_5_out,
       multiplexer_6_out, multiplexer_7_out, multiplexer_8_out, multiplexer_9_out, multiplexer_10_out,
       multiplexer_11_out, multiplexer_12_out, multiplexer_13_out, multiplexer_14_out, multiplexer_15_out,
       multiplexer_16_out;

  Comparator #(.width(3), .mode("unsigned")) comparator_1 (
    .a(3'b000), .b(reg_addr), .eq(comparator_1_eq));  // open: gt, lt
  Comparator #(.width(3), .mode("unsigned")) comparator_2 (
    .a(3'b001), .b(reg_addr), .eq(comparator_2_eq));  // open: gt, lt
  Comparator #(.width(3), .mode("unsigned")) comparator_3 (
    .a(3'b010), .b(reg_addr), .eq(comparator_3_eq));  // open: gt, lt
  Comparator #(.width(3), .mode("unsigned")) comparator_4 (
    .a(3'b011), .b(reg_addr), .eq(comparator_4_eq));  // open: gt, lt
  Comparator #(.width(3), .mode("unsigned")) comparator_5 (
    .a(3'b100), .b(reg_addr), .eq(comparator_5_eq));  // open: gt, lt
  Comparator #(.width(3), .mode("unsigned")) comparator_6 (
    .a(3'b101), .b(reg_addr), .eq(comparator_6_eq));  // open: gt, lt
  Comparator #(.width(3), .mode("unsigned")) comparator_7 (
    .a(3'b110), .b(reg_addr), .eq(comparator_7_eq));  // open: gt, lt
  Comparator #(.width(3), .mode("unsigned")) comparator_8 (
    .a(3'b111), .b(reg_addr), .eq(comparator_8_eq));  // open: gt, lt
  and and_1 (and_1_out, comparator_1_eq, en_reg);
  and and_2 (and_2_out, comparator_2_eq, en_reg);
  and and_3 (and_3_out, comparator_3_eq, en_reg);
  and and_4 (and_4_out, comparator_4_eq, en_reg);
  and and_5 (and_5_out, comparator_5_eq, en_reg);
  and and_6 (and_6_out, comparator_6_eq, en_reg);
  and and_7 (and_7_out, comparator_7_eq, en_reg);
  and and_8 (and_8_out, comparator_8_eq, en_reg);
  Comparator #(.width(3), .mode("unsigned")) comparator_9 (
    .a(3'b000), .b(mem_addr), .eq(comparator_9_eq));  // open: gt, lt
  and and_9 (and_9_out, comparator_9_eq, en_mem);
  Comparator #(.width(3), .mode("unsigned")) comparator_10 (
    .a(3'b001), .b(mem_addr), .eq(comparator_10_eq));  // open: gt, lt
  and and_10 (and_10_out, comparator_10_eq, en_mem);
  Comparator #(.width(3), .mode("unsigned")) comparator_11 (
    .a(3'b010), .b(mem_addr), .eq(comparator_11_eq));  // open: gt, lt
  and and_11 (and_11_out, comparator_11_eq, en_mem);
  Comparator #(.width(3), .mode("unsigned")) comparator_12 (
    .a(3'b011), .b(mem_addr), .eq(comparator_12_eq));  // open: gt, lt
  and and_12 (and_12_out, comparator_12_eq, en_mem);
  Comparator #(.width(3), .mode("unsigned")) comparator_13 (
    .a(3'b100), .b(mem_addr), .eq(comparator_13_eq));  // open: gt, lt
  and and_13 (and_13_out, comparator_13_eq, en_mem);
  Comparator #(.width(3), .mode("unsigned")) comparator_14 (
    .a(3'b101), .b(mem_addr), .eq(comparator_14_eq));  // open: gt, lt
  and and_14 (and_14_out, comparator_14_eq, en_mem);
  Comparator #(.width(3), .mode("unsigned")) comparator_15 (
    .a(3'b110), .b(mem_addr), .eq(comparator_15_eq));  // open: gt, lt
  and and_15 (and_15_out, comparator_15_eq, en_mem);
  Comparator #(.width(3), .mode("unsigned")) comparator_16 (
    .a(3'b111), .b(mem_addr), .eq(comparator_16_eq));  // open: gt, lt
  and and_16 (and_16_out, comparator_16_eq, en_mem);
  Multiplexer #(.width(16), .enable("false")) multiplexer_1 (
    .in0(reg0), .in1(reg_in), .out(multiplexer_1_out), .sel(and_1_out));
  Multiplexer #(.width(16), .enable("false")) multiplexer_2 (
    .in0(reg1), .in1(reg_in), .out(multiplexer_2_out), .sel(and_2_out));
  Multiplexer #(.width(16), .enable("false")) multiplexer_3 (
    .in0(reg2), .in1(reg_in), .out(multiplexer_3_out), .sel(and_3_out));
  Multiplexer #(.width(16), .enable("false")) multiplexer_4 (
    .in0(reg3), .in1(reg_in), .out(multiplexer_4_out), .sel(and_4_out));
  Multiplexer #(.width(16), .enable("false")) multiplexer_5 (
    .in0(reg4), .in1(reg_in), .out(multiplexer_5_out), .sel(and_5_out));
  Multiplexer #(.width(16), .enable("false")) multiplexer_6 (
    .in0(reg5), .in1(reg_in), .out(multiplexer_6_out), .sel(and_6_out));
  Multiplexer #(.width(16), .enable("false")) multiplexer_7 (
    .in0(reg6), .in1(reg_in), .out(multiplexer_7_out), .sel(and_7_out));
  Multiplexer #(.width(16), .enable("false")) multiplexer_8 (
    .in0(reg7), .in1(reg_in), .out(multiplexer_8_out), .sel(and_8_out));
  Register #(.width(16)) register_1 (.D(multiplexer_9_out), .clk(clock), .Q(reg0), .clr(reset));  // open: en
  Multiplexer #(.width(16), .enable("false")) multiplexer_9 (
    .in0(multiplexer_1_out), .in1(mem_in), .out(multiplexer_9_out), .sel(and_9_out));
  Register #(.width(16)) register_2 (.D(multiplexer_10_out), .clk(clock), .Q(reg1), .clr(reset));  // open: en
  Multiplexer #(.width(16), .enable("false")) multiplexer_10 (
    .in0(multiplexer_2_out), .in1(mem_in), .out(multiplexer_10_out), .sel(and_10_out));
  Register #(.width(16)) register_3 (.D(multiplexer_11_out), .clk(clock), .Q(reg2), .clr(reset));  // open: en
  Multiplexer #(.width(16), .enable("false")) multiplexer_11 (
    .in0(multiplexer_3_out), .in1(mem_in), .out(multiplexer_11_out), .sel(and_11_out));
  Register #(.width(16)) register_4 (.D(multiplexer_12_out), .clk(clock), .Q(reg3), .clr(reset));  // open: en
  Multiplexer #(.width(16), .enable("false")) multiplexer_12 (
    .in0(multiplexer_4_out), .in1(mem_in), .out(multiplexer_12_out), .sel(and_12_out));
  Register #(.width(16)) register_5 (.D(multiplexer_13_out), .clk(clock), .Q(reg4), .clr(reset));  // open: en
  Multiplexer #(.width(16), .enable("false")) multiplexer_13 (
    .in0(multiplexer_5_out), .in1(mem_in), .out(multiplexer_13_out), .sel(and_13_out));
  Register #(.width(16)) register_6 (.D(multiplexer_14_out), .clk(clock), .Q(reg5), .clr(reset));  // open: en
  Multiplexer #(.width(16), .enable("false")) multiplexer_14 (
    .in0(multiplexer_6_out), .in1(mem_in), .out(multiplexer_14_out), .sel(and_14_out));
  Register #(.width(16)) register_7 (.D(multiplexer_15_out), .clk(clock), .Q(reg6), .clr(reset));  // open: en
  Multiplexer #(.width(16), .enable("false")) multiplexer_15 (
    .in0(multiplexer_7_out), .in1(mem_in), .out(multiplexer_15_out), .sel(and_15_out));
  Register #(.width(16)) register_8 (.D(multiplexer_16_out), .clk(clock), .Q(reg7), .clr(reset));  // open: en
  Multiplexer #(.width(16), .enable("false")) multiplexer_16 (
    .in0(multiplexer_8_out), .in1(mem_in), .out(multiplexer_16_out), .sel(and_16_out));
  Multiplexer #(.select(3), .width(16), .enable("false")) multiplexer_17 (
    .in0(reg0), .in1(reg1), .in2(reg2), .in3(reg3), .in4(reg4), .in5(reg5), .in6(reg6), .in7(reg7),
    .out(regA_out), .sel(regA_sel));
  Multiplexer #(.select(3), .width(16), .enable("false")) multiplexer_18 (
    .in0(reg0), .in1(reg1), .in2(reg2), .in3(reg3), .in4(reg4), .in5(reg5), .in6(reg6), .in7(reg7),
    .out(regB_out), .sel(regB_sel));
  Multiplexer #(.select(3), .width(16), .enable("false")) multiplexer_19 (
    .in0(reg0), .in1(reg1), .in2(reg2), .in3(reg3), .in4(reg4), .in5(reg5), .in6(reg6), .in7(reg7),
    .out(regC_out), .sel(regC_sel));
endmodule

module cache (
  input  [4:0] addr,
  input  we,
  input  clock,
  input  [15:0] data_in,
  output [15:0] data_out
);

  RAM #(.addrWidth(5), .dataWidth(16), .databus("bibus")) ram_1 (
    .addr(addr), .we(we), .clk(clock), .din(data_in), .dout(data_out));  // open: oe
endmodule

module lifo (
  input  [15:0] data_in,
  input  reset,
  input  clock,
  input  push,
  input  pop,
  output [15:0] data_out,
  output full,
  output empty
);

  wire and_1_out, and_2_out, and_3_out, and_4_out, and_5_out, and_6_out, and_7_out, and_8_out, and_9_out,
       and_10_out, comparator_3_eq, comparator_4_eq, comparator_5_eq, comparator_6_eq, comparator_7_eq,
       comparator_8_eq, comparator_9_eq, comparator_10_eq;
  wire [2:0] adder_1_out, multiplexer_1_out, multiplexer_2_out, register_9_q, subtractor_1_out;
  wire [15:0] register_1_q, register_2_q, register_3_q, register_4_q, register_5_q, register_6_q,
       register_7_q, register_8_q;

  Adder #(.width(3)) adder_1 (.a(register_9_q), .b(3'b001), .out(adder_1_out));  // open: cin, cout
  Subtractor #(.width(3)) subtractor_1 (.a(register_9_q), .b(3'b001), .out(subtractor_1_out));  // open: bin, bout
  Comparator #(.width(3), .mode("unsigned")) comparator_1 (.a(register_9_q), .b(3'b111), .eq(full));  // open: gt, lt
  Comparator #(.width(3), .mode("unsigned")) comparator_2 (.a(register_9_q), .b(3'b000), .eq(empty));  // open: gt, lt
  Comparator #(.width(3), .mode("unsigned")) comparator_3 (
    .a(3'b000), .b(register_9_q), .eq(comparator_3_eq));  // open: gt, lt
  Comparator #(.width(3), .mode("unsigned")) comparator_4 (
    .a(3'b001), .b(register_9_q), .eq(comparator_4_eq));  // open: gt, lt
  Comparator #(.width(3), .mode("unsigned")) comparator_5 (
    .a(3'b010), .b(register_9_q), .eq(comparator_5_eq));  // open: gt, lt
  Comparator #(.width(3), .mode("unsigned")) comparator_6 (
    .a(3'b011), .b(register_9_q), .eq(comparator_6_eq));  // open: gt, lt
  Comparator #(.width(3), .mode("unsigned")) comparator_7 (
    .a(3'b100), .b(register_9_q), .eq(comparator_7_eq));  // open: gt, lt
  Comparator #(.width(3), .mode("unsigned")) comparator_8 (
    .a(3'b101), .b(register_9_q), .eq(comparator_8_eq));  // open: gt, lt
  Comparator #(.width(3), .mode("unsigned")) comparator_9 (
    .a(3'b110), .b(register_9_q), .eq(comparator_9_eq));  // open: gt, lt
  Comparator #(.width(3), .mode("unsigned")) comparator_10 (
    .a(3'b111), .b(register_9_q), .eq(comparator_10_eq));  // open: gt, lt
  Multiplexer #(.width(3), .enable("false")) multiplexer_1 (
    .in0(register_9_q), .in1(adder_1_out), .out(multiplexer_1_out), .sel(and_1_out));
  and and_1 (and_1_out, push, ~full);  // AND_Gate
  and and_2 (and_2_out, pop, ~empty);  // AND_Gate
  Register #(.width(16)) register_1 (.D(data_in), .en(and_3_out), .clk(clock), .Q(register_1_q), .clr(reset));
  and and_3 (and_3_out, comparator_3_eq, push);
  Register #(.width(16)) register_2 (.D(data_in), .en(and_4_out), .clk(clock), .Q(register_2_q), .clr(reset));
  and and_4 (and_4_out, comparator_4_eq, push);
  Register #(.width(16)) register_3 (.D(data_in), .en(and_5_out), .clk(clock), .Q(register_3_q), .clr(reset));
  and and_5 (and_5_out, comparator_5_eq, push);
  Register #(.width(16)) register_4 (.D(data_in), .en(and_6_out), .clk(clock), .Q(register_4_q), .clr(reset));
  and and_6 (and_6_out, comparator_6_eq, push);
  Register #(.width(16)) register_5 (.D(data_in), .en(and_7_out), .clk(clock), .Q(register_5_q), .clr(reset));
  and and_7 (and_7_out, comparator_7_eq, push);
  Register #(.width(16)) register_6 (.D(data_in), .en(and_8_out), .clk(clock), .Q(register_6_q), .clr(reset));
  and and_8 (and_8_out, comparator_8_eq, push);
  Register #(.width(16)) register_7 (.D(data_in), .en(and_9_out), .clk(clock), .Q(register_7_q), .clr(reset));
  and and_9 (and_9_out, comparator_9_eq, push);
  Register #(.width(16)) register_8 (.D(data_in), .en(and_10_out), .clk(clock), .Q(register_8_q), .clr(reset));
  and and_10 (and_10_out, comparator_10_eq, push);
  Register #(.width(3)) register_9 (.D(multiplexer_2_out), .clk(clock), .Q(register_9_q), .clr(reset));  // open: en
  Multiplexer #(.width(3), .enable("false")) multiplexer_2 (
    .in0(multiplexer_1_out), .in1(subtractor_1_out), .out(multiplexer_2_out), .sel(and_2_out));
  Multiplexer #(.select(3), .width(16), .enable("false")) multiplexer_3 (
    .in0(register_1_q), .in1(register_2_q), .in2(register_3_q), .in3(register_4_q), .in4(register_5_q),
    .in5(register_6_q), .in6(register_7_q), .in7(register_8_q), .out(data_out), .sel(register_9_q));
endmodule

module memory_buffer (
  input  [22:0] data_in,
  input  push,
  input  pop,
  input  reset,
  input  clock,
  output [22:0] data_out,
  output full,
  output empty
);

  wire and_1_out, and_2_out, and_3_out, and_4_out, and_5_out, and_6_out, and_7_out, and_8_out, and_9_out,
       and_10_out, comparator_1_eq, comparator_2_eq, comparator_3_eq, comparator_4_eq, comparator_5_eq,
       comparator_6_eq, comparator_7_eq, comparator_8_eq;
  wire [2:0] adder_1_out, adder_2_out, register_9_q, register_10_q;
  wire [22:0] register_1_q, register_2_q, register_3_q, register_4_q, register_5_q, register_6_q,
       register_7_q, register_8_q;

  Comparator #(.width(3), .mode("unsigned")) comparator_1 (
    .a(3'b000), .b(register_9_q), .eq(comparator_1_eq));  // open: gt, lt
  Comparator #(.width(3), .mode("unsigned")) comparator_2 (
    .a(3'b001), .b(register_9_q), .eq(comparator_2_eq));  // open: gt, lt
  Comparator #(.width(3), .mode("unsigned")) comparator_3 (
    .a(3'b010), .b(register_9_q), .eq(comparator_3_eq));  // open: gt, lt
  Comparator #(.width(3), .mode("unsigned")) comparator_4 (
    .a(3'b011), .b(register_9_q), .eq(comparator_4_eq));  // open: gt, lt
  Comparator #(.width(3), .mode("unsigned")) comparator_5 (
    .a(3'b100), .b(register_9_q), .eq(comparator_5_eq));  // open: gt, lt
  Comparator #(.width(3), .mode("unsigned")) comparator_6 (
    .a(3'b101), .b(register_9_q), .eq(comparator_6_eq));  // open: gt, lt
  Comparator #(.width(3), .mode("unsigned")) comparator_7 (
    .a(3'b110), .b(register_9_q), .eq(comparator_7_eq));  // open: gt, lt
  Comparator #(.width(3), .mode("unsigned")) comparator_8 (
    .a(3'b111), .b(register_9_q), .eq(comparator_8_eq));  // open: gt, lt
  Adder #(.width(3)) adder_1 (.a(register_9_q), .b(3'b001), .out(adder_1_out));  // open: cin, cout
  Comparator #(.width(3), .mode("unsigned")) comparator_9 (
    .a(adder_1_out), .b(register_10_q), .eq(full));  // open: gt, lt
  Comparator #(.width(3), .mode("unsigned")) comparator_10 (
    .a(register_10_q), .b(register_9_q), .eq(empty));  // open: gt, lt
  Register #(.width(23)) register_1 (.D(data_in), .en(and_1_out), .clk(clock), .Q(register_1_q), .clr(reset));
  and and_1 (and_1_out, comparator_1_eq, and_9_out);
  Register #(.width(23)) register_2 (.D(data_in), .en(and_2_out), .clk(clock), .Q(register_2_q), .clr(reset));
  and and_2 (and_2_out, comparator_2_eq, and_9_out);
  Register #(.width(23)) register_3 (.D(data_in), .en(and_3_out), .clk(clock), .Q(register_3_q), .clr(reset));
  and and_3 (and_3_out, comparator_3_eq, and_9_out);
  Register #(.width(23)) register_4 (.D(data_in), .en(and_4_out), .clk(clock), .Q(register_4_q), .clr(reset));
  and and_4 (and_4_out, comparator_4_eq, and_9_out);
  Register #(.width(23)) register_5 (.D(data_in), .en(and_5_out), .clk(clock), .Q(register_5_q), .clr(reset));
  and and_5 (and_5_out, comparator_5_eq, and_9_out);
  Register #(.width(23)) register_6 (.D(data_in), .en(and_6_out), .clk(clock), .Q(register_6_q), .clr(reset));
  and and_6 (and_6_out, comparator_6_eq, and_9_out);
  Register #(.width(23)) register_7 (.D(data_in), .en(and_7_out), .clk(clock), .Q(register_7_q), .clr(reset));
  and and_7 (and_7_out, comparator_7_eq, and_9_out);
  Register #(.width(23)) register_8 (.D(data_in), .en(and_8_out), .clk(clock), .Q(register_8_q), .clr(reset));
  and and_8 (and_8_out, comparator_8_eq, and_9_out);
  Register #(.width(3)) register_9 (.D(adder_1_out), .en(and_9_out), .clk(clock), .Q(register_9_q), .clr(reset));
  and and_9 (and_9_out, push, ~full);  // AND_Gate
  Register #(.width(3)) register_10 (.D(adder_2_out), .en(and_10_out), .clk(clock), .Q(register_10_q), .clr(reset));
  Adder #(.width(3)) adder_2 (.a(register_10_q), .b(3'b001), .out(adder_2_out));  // open: cin, cout
  and and_10 (and_10_out, pop, ~empty);  // AND_Gate
  Multiplexer #(.select(3), .width(23), .enable("false")) multiplexer_1 (
    .in0(register_1_q), .in1(register_2_q), .in2(register_3_q), .in3(register_4_q), .in4(register_5_q),
    .in5(register_6_q), .in6(register_7_q), .in7(register_8_q), .out(data_out), .sel(register_10_q));
endmodule

module cache_control (
  input  [15:0] set_addr_16,
  input  cache_access,
  input  reset,
  input  clock,
  output [4:0] miss_addr_5,
  output [4:0] set_addr_5,
  output [15:0] miss_addr_16,
  output hit,
  output miss
);

  wire and_1_out, and_2_out, and_3_out, and_4_out, and_5_out, and_6_out, and_7_out, and_8_out, and_10_out,
       and_11_out, and_12_out, and_13_out, and_14_out, and_15_out, and_16_out, and_17_out, and_18_out,
       and_19_out, and_20_out, and_21_out, and_22_out, and_23_out, and_24_out, and_25_out, comparator_1_eq,
       comparator_2_eq, comparator_3_eq, comparator_4_eq, comparator_5_eq, comparator_6_eq, comparator_7_eq,
       comparator_8_eq, comparator_9_eq, comparator_10_eq, comparator_11_eq, comparator_12_eq,
       comparator_13_eq, comparator_14_eq, comparator_15_eq, comparator_16_eq, comparator_17_eq,
       comparator_18_lt, comparator_19_lt, comparator_20_lt, comparator_21_eq, comparator_22_eq,
       comparator_23_eq, comparator_24_eq, comparator_25_eq, comparator_26_eq, comparator_27_eq,
       comparator_28_eq, comparator_29_eq, comparator_30_eq, comparator_31_eq, comparator_32_eq,
       comparator_33_eq, comparator_34_eq, comparator_35_eq, comparator_36_eq, comparator_37_eq,
       comparator_38_eq, comparator_39_eq, comparator_40_eq, comparator_41_eq, comparator_42_eq,
       comparator_43_eq, comparator_44_eq, multiplexer_20_out, or_1_out;
  wire [1:0] multiplexer_7_out, multiplexer_8_out, multiplexer_9_out, multiplexer_10_out, multiplexer_12_out,
       multiplexer_13_out, multiplexer_14_out, multiplexer_15_out, multiplexer_16_out, multiplexer_17_out,
       multiplexer_18_out, multiplexer_19_out, multiplexer_21_out, multiplexer_22_out, multiplexer_23_out,
       multiplexer_28_out, multiplexer_28_out_2, multiplexer_28_out_3;
  wire [3:0] multiplexer_24_out, multiplexer_29_out, register_17_q, register_18_q, register_19_q,
       register_20_q, register_21_q, register_22_q, register_23_q, register_24_q;
  wire [7:0] multiplexer_2_out, multiplexer_3_out, multiplexer_4_out, multiplexer_5_out, register_9_q,
       register_10_q, register_11_q, register_12_q, register_13_q, register_14_q, register_15_q,
       register_16_q;
  wire [15:0] shifter_2_out;
  wire [15:3] shifter_1_out;
  wire [31:0] multiplexer_6_out, register_1_q, register_2_q, register_3_q, register_4_q, register_5_q,
       register_6_q, register_7_q, register_8_q;

  Shifter #(.width(16), .shift("lr")) shifter_1 (
    .in(set_addr_16), .\dist (4'b0101), .out({shifter_1_out, miss_addr_5[4:2]}));
  Multiplexer #(.select(2), .width(8), .enable("false")) multiplexer_1 (
    .in0(multiplexer_6_out[7:0]), .in1(multiplexer_6_out[15:8]), .in2(multiplexer_6_out[23:16]),
    .in3(multiplexer_6_out[31:24]), .out(miss_addr_16[15:8]), .sel(miss_addr_5[1:0]));
  Shifter #(.width(16), .shift("lr")) shifter_2 (
    .in({shifter_1_out, miss_addr_5[4:2]}), .\dist (4'b0011), .out(shifter_2_out));
  Comparator #(.width(2)) comparator_1 (.a(miss_addr_5[1:0]), .b(2'b00), .eq(comparator_1_eq));  // open: gt, lt
  Comparator #(.width(2)) comparator_2 (.a(miss_addr_5[1:0]), .b(2'b01), .eq(comparator_2_eq));  // open: gt, lt
  Comparator #(.width(2)) comparator_3 (.a(miss_addr_5[1:0]), .b(2'b10), .eq(comparator_3_eq));  // open: gt, lt
  Comparator #(.width(2)) comparator_4 (.a(miss_addr_5[1:0]), .b(2'b11), .eq(comparator_4_eq));  // open: gt, lt
  Multiplexer #(.width(8), .enable("false")) multiplexer_2 (
    .in0(multiplexer_6_out[7:0]), .in1(shifter_2_out[7:0]), .out(multiplexer_2_out), .sel(comparator_1_eq));
  Multiplexer #(.width(8), .enable("false")) multiplexer_3 (
    .in0(multiplexer_6_out[15:8]), .in1(shifter_2_out[7:0]), .out(multiplexer_3_out), .sel(comparator_2_eq));
  Multiplexer #(.width(8), .enable("false")) multiplexer_4 (
    .in0(multiplexer_6_out[23:16]), .in1(shifter_2_out[7:0]), .out(multiplexer_4_out), .sel(comparator_3_eq));
  Multiplexer #(.width(8), .enable("false")) multiplexer_5 (
    .in0(multiplexer_6_out[31:24]), .in1(shifter_2_out[7:0]), .out(multiplexer_5_out), .sel(comparator_4_eq));
  Comparator #(.width(3), .mode("unsigned")) comparator_5 (
    .a(3'b000), .b(miss_addr_5[4:2]), .eq(comparator_5_eq));  // open: gt, lt
  and and_1 (and_1_out, comparator_5_eq, cache_access);
  Comparator #(.width(3), .mode("unsigned")) comparator_6 (
    .a(3'b001), .b(miss_addr_5[4:2]), .eq(comparator_6_eq));  // open: gt, lt
  and and_2 (and_2_out, comparator_6_eq, cache_access);
  Comparator #(.width(3), .mode("unsigned")) comparator_7 (
    .a(3'b010), .b(miss_addr_5[4:2]), .eq(comparator_7_eq));  // open: gt, lt
  and and_3 (and_3_out, comparator_7_eq, cache_access);
  Comparator #(.width(3), .mode("unsigned")) comparator_8 (
    .a(3'b011), .b(miss_addr_5[4:2]), .eq(comparator_8_eq));  // open: gt, lt
  and and_4 (and_4_out, comparator_8_eq, cache_access);
  Comparator #(.width(3), .mode("unsigned")) comparator_9 (
    .a(3'b100), .b(miss_addr_5[4:2]), .eq(comparator_9_eq));  // open: gt, lt
  and and_5 (and_5_out, comparator_9_eq, cache_access);
  Comparator #(.width(3), .mode("unsigned")) comparator_10 (
    .a(3'b101), .b(miss_addr_5[4:2]), .eq(comparator_10_eq));  // open: gt, lt
  and and_6 (and_6_out, comparator_10_eq, cache_access);
  Comparator #(.width(3), .mode("unsigned")) comparator_11 (
    .a(3'b110), .b(miss_addr_5[4:2]), .eq(comparator_11_eq));  // open: gt, lt
  and and_7 (and_7_out, comparator_11_eq, cache_access);
  Comparator #(.width(3), .mode("unsigned")) comparator_12 (
    .a(3'b111), .b(miss_addr_5[4:2]), .eq(comparator_12_eq));  // open: gt, lt
  and and_8 (and_8_out, comparator_12_eq, cache_access);
  Register #(.width(32)) register_1 (
    .D({multiplexer_5_out, multiplexer_4_out, multiplexer_3_out, multiplexer_2_out}), .en(and_1_out),
    .clk(clock), .Q(register_1_q), .clr(reset));
  Register #(.width(32)) register_2 (
    .D({multiplexer_5_out, multiplexer_4_out, multiplexer_3_out, multiplexer_2_out}), .en(and_2_out),
    .clk(clock), .Q(register_2_q), .clr(reset));
  Register #(.width(32)) register_3 (
    .D({multiplexer_5_out, multiplexer_4_out, multiplexer_3_out, multiplexer_2_out}), .en(and_3_out),
    .clk(clock), .Q(register_3_q), .clr(reset));
  Register #(.width(32)) register_4 (
    .D({multiplexer_5_out, multiplexer_4_out, multiplexer_3_out, multiplexer_2_out}), .en(and_4_out),
    .clk(clock), .Q(register_4_q), .clr(reset));
  Register #(.width(32)) register_5 (
    .D({multiplexer_5_out, multiplexer_4_out, multiplexer_3_out, multiplexer_2_out}), .en(and_5_out),
    .clk(clock), .Q(register_5_q), .clr(reset));
  Register #(.width(32)) register_6 (
    .D({multiplexer_5_out, multiplexer_4_out, multiplexer_3_out, multiplexer_2_out}), .en(and_6_out),
    .clk(clock), .Q(register_6_q), .clr(reset));
  Register #(.width(32)) register_7 (
    .D({multiplexer_5_out, multiplexer_4_out, multiplexer_3_out, multiplexer_2_out}), .en(and_7_out),
    .clk(clock), .Q(register_7_q), .clr(reset));
  Register #(.width(32)) register_8 (
    .D({multiplexer_5_out, multiplexer_4_out, multiplexer_3_out, multiplexer_2_out}), .en(and_8_out),
    .clk(clock), .Q(register_8_q), .clr(reset));
  Multiplexer #(.select(3), .width(32), .enable("false")) multiplexer_6 (
    .in0(register_1_q), .in1(register_2_q), .in2(register_3_q), .in3(register_4_q), .in4(register_5_q),
    .in5(register_6_q), .in6(register_7_q), .in7(register_8_q), .out(multiplexer_6_out),
    .sel(miss_addr_5[4:2]));
  Comparator comparator_13 (.a(shifter_2_out[7:0]), .b(multiplexer_6_out[7:0]), .eq(comparator_13_eq));  // open: gt, lt
  Comparator comparator_14 (
    .a(shifter_2_out[7:0]), .b(multiplexer_6_out[15:8]), .eq(comparator_14_eq));  // open: gt, lt
  Comparator comparator_15 (
    .a(shifter_2_out[7:0]), .b(multiplexer_6_out[23:16]), .eq(comparator_15_eq));  // open: gt, lt
  Comparator comparator_16 (
    .a(shifter_2_out[7:0]), .b(multiplexer_6_out[31:24]), .eq(comparator_16_eq));  // open: gt, lt
  Multiplexer #(.width(2), .enable("false")) multiplexer_7 (
    .in0(2'b00), .in1(2'b00), .out(multiplexer_7_out), .sel(comparator_16_eq));
  Multiplexer #(.width(2), .enable("false")) multiplexer_8 (
    .in0(multiplexer_7_out), .in1(2'b01), .out(multiplexer_8_out), .sel(comparator_15_eq));
  Multiplexer #(.width(2), .enable("false")) multiplexer_9 (
    .in0(multiplexer_8_out), .in1(2'b10), .out(multiplexer_9_out), .sel(comparator_14_eq));
  or or_1 (or_1_out, comparator_13_eq, comparator_14_eq, comparator_15_eq, comparator_16_eq);
  Multiplexer #(.width(2), .enable("false")) multiplexer_10 (
    .in0(2'b00), .in1(2'b11), .out(multiplexer_10_out), .sel(comparator_16_eq));
  Multiplexer #(.width(2), .enable("false")) multiplexer_11 (
    .in0(multiplexer_9_out), .in1(2'b11), .out(set_addr_5[1:0]), .sel(comparator_13_eq));
  and and_9 (hit, multiplexer_20_out, or_1_out);
  Multiplexer #(.width(2), .enable("false")) multiplexer_12 (
    .in0(multiplexer_10_out), .in1(2'b10), .out(multiplexer_12_out), .sel(comparator_15_eq));
  Multiplexer #(.width(2), .enable("false")) multiplexer_13 (
    .in0(multiplexer_12_out), .in1(2'b01), .out(multiplexer_13_out), .sel(comparator_14_eq));
  Comparator #(.width(2), .mode("unsigned")) comparator_17 (
    .a(multiplexer_23_out), .b(2'b00), .eq(comparator_17_eq));  // open: gt, lt
  Comparator #(.width(2), .mode("unsigned")) comparator_18 (
    .a(multiplexer_23_out), .b(2'b01), .lt(comparator_18_lt));  // open: gt, eq
  Comparator #(.width(2), .mode("unsigned")) comparator_19 (
    .a(multiplexer_23_out), .b(2'b10), .lt(comparator_19_lt));  // open: gt, eq
  Comparator #(.width(2), .mode("unsigned")) comparator_20 (
    .a(multiplexer_23_out), .b(2'b11), .lt(comparator_20_lt));  // open: gt, eq
  not not_1 (miss, hit);
  Multiplexer #(.width(2), .enable("false")) multiplexer_14 (
    .in0(multiplexer_13_out), .in1(2'b00), .out(multiplexer_14_out), .sel(comparator_13_eq));
  Comparator #(.width(2)) comparator_21 (
    .a(multiplexer_14_out), .b(miss_addr_5[1:0]), .eq(comparator_21_eq));  // open: gt, lt
  Comparator #(.width(2)) comparator_22 (
    .a(multiplexer_14_out), .b(multiplexer_28_out_3), .eq(comparator_22_eq));  // open: gt, lt
  Comparator #(.width(2)) comparator_23 (
    .a(multiplexer_14_out), .b(multiplexer_28_out_2), .eq(comparator_23_eq));  // open: gt, lt
  Comparator #(.width(2)) comparator_24 (
    .a(multiplexer_14_out), .b(multiplexer_28_out), .eq(comparator_24_eq));  // open: gt, lt
  Multiplexer #(.width(2), .enable("false")) multiplexer_15 (
    .in0(multiplexer_28_out), .in1(multiplexer_14_out), .out(multiplexer_15_out), .sel(comparator_17_eq));
  Multiplexer #(.width(2), .enable("false")) multiplexer_16 (
    .in0(multiplexer_28_out), .in1(multiplexer_28_out_2), .out(multiplexer_16_out), .sel(comparator_18_lt));
  Multiplexer #(.width(2), .enable("false")) multiplexer_17 (
    .in0(multiplexer_28_out_2), .in1(multiplexer_28_out_3), .out(multiplexer_17_out), .sel(comparator_19_lt));
  Multiplexer #(.width(2), .enable("false")) multiplexer_18 (
    .in0(multiplexer_28_out_3), .in1(miss_addr_5[1:0]), .out(multiplexer_18_out), .sel(comparator_20_lt));
  Multiplexer #(.width(2), .enable("false")) multiplexer_19 (
    .in0(2'b00), .in1(2'b11), .out(multiplexer_19_out), .sel(comparator_21_eq));
  Multiplexer #(.select(2), .enable("false")) multiplexer_20 (
    .in0(multiplexer_29_out[0]), .in1(multiplexer_29_out[1]), .in2(multiplexer_29_out[2]),
    .in3(multiplexer_29_out[3]), .out(multiplexer_20_out), .sel(miss_addr_5[1:0]));
  Multiplexer #(.width(2), .enable("false")) multiplexer_21 (
    .in0(multiplexer_19_out), .in1(2'b10), .out(multiplexer_21_out), .sel(comparator_22_eq));
  Multiplexer #(.width(2), .enable("false")) multiplexer_22 (
    .in0(multiplexer_21_out), .in1(2'b01), .out(multiplexer_22_out), .sel(comparator_23_eq));
  Multiplexer #(.width(2), .enable("false")) multiplexer_23 (
    .in0(multiplexer_22_out), .in1(2'b00), .out(multiplexer_23_out), .sel(comparator_24_eq));
  Comparator #(.width(3), .mode("unsigned")) comparator_25 (
    .a(3'b000), .b(miss_addr_5[4:2]), .eq(comparator_25_eq));  // open: gt, lt
  and and_10 (and_10_out, comparator_25_eq, cache_access);
  Comparator #(.width(3), .mode("unsigned")) comparator_26 (
    .a(3'b001), .b(miss_addr_5[4:2]), .eq(comparator_26_eq));  // open: gt, lt
  and and_11 (and_11_out, comparator_26_eq, cache_access);
  Comparator #(.width(3), .mode("unsigned")) comparator_27 (
    .a(3'b010), .b(miss_addr_5[4:2]), .eq(comparator_27_eq));  // open: gt, lt
  and and_12 (and_12_out, comparator_27_eq, cache_access);
  Comparator #(.width(3), .mode("unsigned")) comparator_28 (
    .a(3'b011), .b(miss_addr_5[4:2]), .eq(comparator_28_eq));  // open: gt, lt
  and and_13 (and_13_out, comparator_28_eq, cache_access);
  Comparator #(.width(3), .mode("unsigned")) comparator_29 (
    .a(3'b100), .b(miss_addr_5[4:2]), .eq(comparator_29_eq));  // open: gt, lt
  and and_14 (and_14_out, comparator_29_eq, cache_access);
  Comparator #(.width(3), .mode("unsigned")) comparator_30 (
    .a(3'b101), .b(miss_addr_5[4:2]), .eq(comparator_30_eq));  // open: gt, lt
  and and_15 (and_15_out, comparator_30_eq, cache_access);
  Comparator #(.width(3), .mode("unsigned")) comparator_31 (
    .a(3'b110), .b(miss_addr_5[4:2]), .eq(comparator_31_eq));  // open: gt, lt
  and and_16 (and_16_out, comparator_31_eq, cache_access);
  Comparator #(.width(3), .mode("unsigned")) comparator_32 (
    .a(3'b111), .b(miss_addr_5[4:2]), .eq(comparator_32_eq));  // open: gt, lt
  and and_17 (and_17_out, comparator_32_eq, cache_access);
  Comparator #(.width(2)) comparator_33 (.a(miss_addr_5[1:0]), .b(2'b00), .eq(comparator_33_eq));  // open: gt, lt
  Comparator #(.width(2)) comparator_34 (.a(miss_addr_5[1:0]), .b(2'b01), .eq(comparator_34_eq));  // open: gt, lt
  Comparator #(.width(2)) comparator_35 (.a(miss_addr_5[1:0]), .b(2'b10), .eq(comparator_35_eq));  // open: gt, lt
  Comparator #(.width(2)) comparator_36 (.a(miss_addr_5[1:0]), .b(2'b11), .eq(comparator_36_eq));  // open: gt, lt
  Register register_9 (
    .D({multiplexer_18_out, multiplexer_17_out, multiplexer_16_out, multiplexer_15_out}), .en(and_10_out),
    .clk(clock), .Q(register_9_q), .clr(reset));
  Register register_10 (
    .D({multiplexer_18_out, multiplexer_17_out, multiplexer_16_out, multiplexer_15_out}), .en(and_11_out),
    .clk(clock), .Q(register_10_q), .clr(reset));
  Register register_11 (
    .D({multiplexer_18_out, multiplexer_17_out, multiplexer_16_out, multiplexer_15_out}), .en(and_12_out),
    .clk(clock), .Q(register_11_q), .clr(reset));
  Register register_12 (
    .D({multiplexer_18_out, multiplexer_17_out, multiplexer_16_out, multiplexer_15_out}), .en(and_13_out),
    .clk(clock), .Q(register_12_q), .clr(reset));
  Register register_13 (
    .D({multiplexer_18_out, multiplexer_17_out, multiplexer_16_out, multiplexer_15_out}), .en(and_14_out),
    .clk(clock), .Q(register_13_q), .clr(reset));
  Register register_14 (
    .D({multiplexer_18_out, multiplexer_17_out, multiplexer_16_out, multiplexer_15_out}), .en(and_15_out),
    .clk(clock), .Q(register_14_q), .clr(reset));
  Register register_15 (
    .D({multiplexer_18_out, multiplexer_17_out, multiplexer_16_out, multiplexer_15_out}), .en(and_16_out),
    .clk(clock), .Q(register_15_q), .clr(reset));
  Register register_16 (
    .D({multiplexer_18_out, multiplexer_17_out, multiplexer_16_out, multiplexer_15_out}), .en(and_17_out),
    .clk(clock), .Q(register_16_q), .clr(reset));
  Multiplexer #(.enable("false")) multiplexer_24 (
    .in0(multiplexer_29_out[0]), .in1(1'b1), .out(multiplexer_24_out[0]), .sel(comparator_33_eq));
  Multiplexer #(.enable("false")) multiplexer_25 (
    .in0(multiplexer_29_out[1]), .in1(1'b1), .out(multiplexer_24_out[1]), .sel(comparator_34_eq));
  Multiplexer #(.enable("false")) multiplexer_26 (
    .in0(multiplexer_29_out[2]), .in1(1'b1), .out(multiplexer_24_out[2]), .sel(comparator_35_eq));
  Multiplexer #(.enable("false")) multiplexer_27 (
    .in0(multiplexer_29_out[3]), .in1(1'b1), .out(multiplexer_24_out[3]), .sel(comparator_36_eq));
  Multiplexer #(.select(3), .width(8), .enable("false")) multiplexer_28 (
    .in0(register_9_q), .in1(register_10_q), .in2(register_11_q), .in3(register_12_q), .in4(register_13_q),
    .in5(register_14_q), .in6(register_15_q), .in7(register_16_q),
    .out({miss_addr_5[1:0], multiplexer_28_out_3, multiplexer_28_out_2, multiplexer_28_out}),
    .sel(miss_addr_5[4:2]));
  Comparator #(.width(3), .mode("unsigned")) comparator_37 (
    .a(3'b000), .b(miss_addr_5[4:2]), .eq(comparator_37_eq));  // open: gt, lt
  Comparator #(.width(3), .mode("unsigned")) comparator_38 (
    .a(3'b001), .b(miss_addr_5[4:2]), .eq(comparator_38_eq));  // open: gt, lt
  Comparator #(.width(3), .mode("unsigned")) comparator_39 (
    .a(3'b010), .b(miss_addr_5[4:2]), .eq(comparator_39_eq));  // open: gt, lt
  Comparator #(.width(3), .mode("unsigned")) comparator_40 (
    .a(3'b011), .b(miss_addr_5[4:2]), .eq(comparator_40_eq));  // open: gt, lt
  Comparator #(.width(3), .mode("unsigned")) comparator_41 (
    .a(3'b100), .b(miss_addr_5[4:2]), .eq(comparator_41_eq));  // open: gt, lt
  Comparator #(.width(3), .mode("unsigned")) comparator_42 (
    .a(3'b101), .b(miss_addr_5[4:2]), .eq(comparator_42_eq));  // open: gt, lt
  Comparator #(.width(3), .mode("unsigned")) comparator_43 (
    .a(3'b110), .b(miss_addr_5[4:2]), .eq(comparator_43_eq));  // open: gt, lt
  Comparator #(.width(3), .mode("unsigned")) comparator_44 (
    .a(3'b111), .b(miss_addr_5[4:2]), .eq(comparator_44_eq));  // open: gt, lt
  Register #(.width(4)) register_17 (
    .D(multiplexer_24_out), .en(and_18_out), .clk(clock), .Q(register_17_q), .clr(reset));
  and and_18 (and_18_out, comparator_37_eq, cache_access);
  Register #(.width(4)) register_18 (
    .D(multiplexer_24_out), .en(and_19_out), .clk(clock), .Q(register_18_q), .clr(reset));
  and and_19 (and_19_out, comparator_38_eq, cache_access);
  Register #(.width(4)) register_19 (
    .D(multiplexer_24_out), .en(and_20_out), .clk(clock), .Q(register_19_q), .clr(reset));
  and and_20 (and_20_out, comparator_39_eq, cache_access);
  Register #(.width(4)) register_20 (
    .D(multiplexer_24_out), .en(and_21_out), .clk(clock), .Q(register_20_q), .clr(reset));
  and and_21 (and_21_out, comparator_40_eq, cache_access);
  Register #(.width(4)) register_21 (
    .D(multiplexer_24_out), .en(and_22_out), .clk(clock), .Q(register_21_q), .clr(reset));
  and and_22 (and_22_out, comparator_41_eq, cache_access);
  Register #(.width(4)) register_22 (
    .D(multiplexer_24_out), .en(and_23_out), .clk(clock), .Q(register_22_q), .clr(reset));
  and and_23 (and_23_out, comparator_42_eq, cache_access);
  Register #(.width(4)) register_23 (
    .D(multiplexer_24_out), .en(and_24_out), .clk(clock), .Q(register_23_q), .clr(reset));
  and and_24 (and_24_out, comparator_43_eq, cache_access);
  Register #(.width(4)) register_24 (
    .D(multiplexer_24_out), .en(and_25_out), .clk(clock), .Q(register_24_q), .clr(reset));
  and and_25 (and_25_out, comparator_44_eq, cache_access);
  Multiplexer #(.select(3), .width(4), .enable("false")) multiplexer_29 (
    .in0(register_17_q), .in1(register_18_q), .in2(register_19_q), .in3(register_20_q), .in4(register_21_q),
    .in5(register_22_q), .in6(register_23_q), .in7(register_24_q), .out(multiplexer_29_out),
    .sel(miss_addr_5[4:2]));

  assign miss_addr_16[7:0] = {miss_addr_5[4:2], {5{1'b0}}};
  assign set_addr_5[4:2] = miss_addr_5[4:2];
endmodule

module data_memory (
  input  [15:0] addr,
  input  we,
  input  clock,
  input  [15:0] datain,
  output [15:0] data_out
);

  RAM #(.addrWidth(16), .dataWidth(16), .databus("bibus")) ram_1 (
    .addr(addr), .we(we), .clk(clock), .din(datain), .dout(data_out));  // open: oe
endmodule

module rs1_fifo (
  input  [2:0] reg_in,
  input  [2:0] mem_in,
  input  push_mem,
  input  push_reg,
  input  reset,
  input  clock,
  output [2:0] reg_out
);

  wire and_1_out, and_2_out, and_3_out, and_4_out, and_5_out, and_6_out, and_7_out, and_8_out, and_9_out,
       and_10_out, and_11_out, and_12_out, and_13_out, and_14_out, and_15_out, and_16_out, and_17_out,
       and_18_out, comparator_1_eq, comparator_2_eq, comparator_3_eq, comparator_4_eq, comparator_5_eq,
       comparator_6_eq, comparator_7_eq, comparator_8_eq, comparator_9_eq, comparator_10_eq,
       comparator_11_eq, comparator_12_eq, comparator_13_eq, comparator_14_eq, comparator_15_eq,
       comparator_16_eq, comparator_17_eq, comparator_18_eq, not_1_out, or_1_out;
  wire [2:0] adder_1_out, adder_2_out, adder_3_out, multiplexer_1_out, multiplexer_2_out, multiplexer_3_out,
       multiplexer_4_out, multiplexer_5_out, multiplexer_6_out, multiplexer_7_out, multiplexer_8_out,
       multiplexer_9_out, multiplexer_10_out, multiplexer_11_out, multiplexer_12_out, multiplexer_13_out,
       multiplexer_14_out, multiplexer_15_out, multiplexer_16_out, multiplexer_17_out, multiplexer_18_out,
       multiplexer_19_out, multiplexer_20_out, register_1_q, register_2_q, register_3_q, register_4_q,
       register_5_q, register_6_q, register_7_q, register_8_q, register_9_q, register_10_q;

  Comparator #(.width(3), .mode("unsigned")) comparator_1 (
    .a(3'b000), .b(register_9_q), .eq(comparator_1_eq));  // open: gt, lt
  and and_1 (and_1_out, comparator_1_eq, and_17_out);
  Comparator #(.width(3), .mode("unsigned")) comparator_2 (
    .a(3'b001), .b(register_9_q), .eq(comparator_2_eq));  // open: gt, lt
  and and_2 (and_2_out, comparator_2_eq, and_17_out);
  Comparator #(.width(3), .mode("unsigned")) comparator_3 (
    .a(3'b010), .b(register_9_q), .eq(comparator_3_eq));  // open: gt, lt
  and and_3 (and_3_out, comparator_3_eq, and_17_out);
  Comparator #(.width(3), .mode("unsigned")) comparator_4 (
    .a(3'b011), .b(register_9_q), .eq(comparator_4_eq));  // open: gt, lt
  and and_4 (and_4_out, comparator_4_eq, and_17_out);
  Comparator #(.width(3), .mode("unsigned")) comparator_5 (
    .a(3'b100), .b(register_9_q), .eq(comparator_5_eq));  // open: gt, lt
  and and_5 (and_5_out, comparator_5_eq, and_17_out);
  Comparator #(.width(3), .mode("unsigned")) comparator_6 (
    .a(3'b101), .b(register_9_q), .eq(comparator_6_eq));  // open: gt, lt
  and and_6 (and_6_out, comparator_6_eq, and_17_out);
  Comparator #(.width(3), .mode("unsigned")) comparator_7 (
    .a(3'b110), .b(register_9_q), .eq(comparator_7_eq));  // open: gt, lt
  and and_7 (and_7_out, comparator_7_eq, and_17_out);
  Comparator #(.width(3), .mode("unsigned")) comparator_8 (
    .a(3'b111), .b(register_9_q), .eq(comparator_8_eq));  // open: gt, lt
  and and_8 (and_8_out, comparator_8_eq, and_17_out);
  Adder #(.width(3)) adder_1 (.a(register_9_q), .b(3'b001), .out(adder_1_out));  // open: cin, cout
  Adder #(.width(3)) adder_2 (.a(register_9_q), .b(3'b010), .out(adder_2_out));  // open: cin, cout
  Comparator #(.width(3), .mode("unsigned")) comparator_9 (
    .a(3'b000), .b(adder_1_out), .eq(comparator_9_eq));  // open: gt, lt
  Comparator #(.width(3), .mode("unsigned")) comparator_10 (
    .a(3'b001), .b(adder_1_out), .eq(comparator_10_eq));  // open: gt, lt
  Comparator #(.width(3), .mode("unsigned")) comparator_11 (
    .a(3'b010), .b(adder_1_out), .eq(comparator_11_eq));  // open: gt, lt
  Comparator #(.width(3), .mode("unsigned")) comparator_12 (
    .a(3'b011), .b(adder_1_out), .eq(comparator_12_eq));  // open: gt, lt
  Comparator #(.width(3), .mode("unsigned")) comparator_13 (
    .a(3'b100), .b(adder_1_out), .eq(comparator_13_eq));  // open: gt, lt
  Comparator #(.width(3), .mode("unsigned")) comparator_14 (
    .a(3'b101), .b(adder_1_out), .eq(comparator_14_eq));  // open: gt, lt
  Comparator #(.width(3), .mode("unsigned")) comparator_15 (
    .a(3'b110), .b(adder_1_out), .eq(comparator_15_eq));  // open: gt, lt
  Comparator #(.width(3), .mode("unsigned")) comparator_16 (
    .a(3'b111), .b(adder_1_out), .eq(comparator_16_eq));  // open: gt, lt
  Comparator #(.width(3), .mode("unsigned")) comparator_17 (
    .a(adder_1_out), .b(register_10_q), .eq(comparator_17_eq));  // open: gt, lt
  and and_9 (and_9_out, comparator_9_eq, and_18_out);
  and and_10 (and_10_out, comparator_10_eq, and_18_out);
  and and_11 (and_11_out, comparator_11_eq, and_18_out);
  and and_12 (and_12_out, comparator_12_eq, and_18_out);
  and and_13 (and_13_out, comparator_13_eq, and_18_out);
  and and_14 (and_14_out, comparator_14_eq, and_18_out);
  and and_15 (and_15_out, comparator_15_eq, and_18_out);
  and and_16 (and_16_out, comparator_16_eq, and_18_out);
  or or_1 (or_1_out, push_reg, push_mem);
  Multiplexer #(.width(3), .enable("false")) multiplexer_1 (
    .in0(register_1_q), .in1(multiplexer_9_out), .out(multiplexer_1_out), .sel(and_1_out));
  Multiplexer #(.width(3), .enable("false")) multiplexer_2 (
    .in0(register_2_q), .in1(multiplexer_9_out), .out(multiplexer_2_out), .sel(and_2_out));
  Multiplexer #(.width(3), .enable("false")) multiplexer_3 (
    .in0(register_3_q), .in1(multiplexer_9_out), .out(multiplexer_3_out), .sel(and_3_out));
  Multiplexer #(.width(3), .enable("false")) multiplexer_4 (
    .in0(register_4_q), .in1(multiplexer_9_out), .out(multiplexer_4_out), .sel(and_4_out));
  Multiplexer #(.width(3), .enable("false")) multiplexer_5 (
    .in0(register_5_q), .in1(multiplexer_9_out), .out(multiplexer_5_out), .sel(and_5_out));
  Multiplexer #(.width(3), .enable("false")) multiplexer_6 (
    .in0(register_6_q), .in1(multiplexer_9_out), .out(multiplexer_6_out), .sel(and_6_out));
  Multiplexer #(.width(3), .enable("false")) multiplexer_7 (
    .in0(register_7_q), .in1(multiplexer_9_out), .out(multiplexer_7_out), .sel(and_7_out));
  Multiplexer #(.width(3), .enable("false")) multiplexer_8 (
    .in0(register_8_q), .in1(multiplexer_9_out), .out(multiplexer_8_out), .sel(and_8_out));
  Multiplexer #(.width(3), .enable("false")) multiplexer_9 (
    .in0(reg_in), .in1(mem_in), .out(multiplexer_9_out), .sel(push_mem));
  Multiplexer #(.width(3), .enable("false")) multiplexer_10 (
    .in0(register_9_q), .in1(adder_1_out), .out(multiplexer_10_out), .sel(and_17_out));
  and and_17 (and_17_out, or_1_out, ~comparator_17_eq);  // AND_Gate
  and and_18 (and_18_out, push_mem, push_reg, ~comparator_17_eq);  // AND_Gate
  Comparator #(.width(3), .mode("unsigned")) comparator_18 (
    .a(register_10_q), .b(register_9_q), .eq(comparator_18_eq));  // open: gt, lt
  Multiplexer #(.width(3), .enable("false")) multiplexer_11 (
    .in0(multiplexer_1_out), .in1(reg_in), .out(multiplexer_11_out), .sel(and_9_out));
  Multiplexer #(.width(3), .enable("false")) multiplexer_12 (
    .in0(multiplexer_2_out), .in1(reg_in), .out(multiplexer_12_out), .sel(and_10_out));
  Multiplexer #(.width(3), .enable("false")) multiplexer_13 (
    .in0(multiplexer_3_out), .in1(reg_in), .out(multiplexer_13_out), .sel(and_11_out));
  Multiplexer #(.width(3), .enable("false")) multiplexer_14 (
    .in0(multiplexer_4_out), .in1(reg_in), .out(multiplexer_14_out), .sel(and_12_out));
  Multiplexer #(.width(3), .enable("false")) multiplexer_15 (
    .in0(multiplexer_5_out), .in1(reg_in), .out(multiplexer_15_out), .sel(and_13_out));
  Multiplexer #(.width(3), .enable("false")) multiplexer_16 (
    .in0(multiplexer_6_out), .in1(reg_in), .out(multiplexer_16_out), .sel(and_14_out));
  Multiplexer #(.width(3), .enable("false")) multiplexer_17 (
    .in0(multiplexer_7_out), .in1(reg_in), .out(multiplexer_17_out), .sel(and_15_out));
  Multiplexer #(.width(3), .enable("false")) multiplexer_18 (
    .in0(multiplexer_8_out), .in1(reg_in), .out(multiplexer_18_out), .sel(and_16_out));
  Multiplexer #(.width(3), .enable("false")) multiplexer_19 (
    .in0(multiplexer_10_out), .in1(adder_2_out), .out(multiplexer_19_out), .sel(and_18_out));
  Adder #(.width(3)) adder_3 (.a(register_10_q), .b(3'b001), .out(adder_3_out));  // open: cin, cout
  not not_1 (not_1_out, comparator_18_eq);
  Register #(.width(3)) register_1 (.D(multiplexer_11_out), .clk(clock), .Q(register_1_q), .clr(reset));  // open: en
  Register #(.width(3)) register_2 (.D(multiplexer_12_out), .clk(clock), .Q(register_2_q), .clr(reset));  // open: en
  Register #(.width(3)) register_3 (.D(multiplexer_13_out), .clk(clock), .Q(register_3_q), .clr(reset));  // open: en
  Register #(.width(3)) register_4 (.D(multiplexer_14_out), .clk(clock), .Q(register_4_q), .clr(reset));  // open: en
  Register #(.width(3)) register_5 (.D(multiplexer_15_out), .clk(clock), .Q(register_5_q), .clr(reset));  // open: en
  Register #(.width(3)) register_6 (.D(multiplexer_16_out), .clk(clock), .Q(register_6_q), .clr(reset));  // open: en
  Register #(.width(3)) register_7 (.D(multiplexer_17_out), .clk(clock), .Q(register_7_q), .clr(reset));  // open: en
  Register #(.width(3)) register_8 (.D(multiplexer_18_out), .clk(clock), .Q(register_8_q), .clr(reset));  // open: en
  Register #(.width(3)) register_9 (.D(multiplexer_19_out), .clk(clock), .Q(register_9_q), .clr(reset));  // open: en
  Register #(.width(3)) register_10 (.D(adder_3_out), .en(not_1_out), .clk(clock), .Q(register_10_q), .clr(reset));
  Multiplexer #(.select(3), .width(3), .enable("false")) multiplexer_20 (
    .in0(register_1_q), .in1(register_2_q), .in2(register_3_q), .in3(register_4_q), .in4(register_5_q),
    .in5(register_6_q), .in6(register_7_q), .in7(register_8_q), .out(multiplexer_20_out), .sel(register_10_q));
  Multiplexer #(.width(3), .enable("false")) multiplexer_21 (
    .in0(multiplexer_20_out), .in1(3'b000), .out(reg_out), .sel(comparator_18_eq));
endmodule

module RAT_control (
  input  read_miss,
  input  write_miss,
  input  read_hit,
  input  unset,
  input  set,
  input  [2:0] addr_used,
  input  enable,
  input  [2:0] addr_unused,
  input  reset,
  input  clock,
  output rm_delay,
  output wm_delay,
  output rh_delay,
  output pause,
  output [7:0] instr_buffer_stat_reg,
  output [2:0] free_addr
);

  wire and_1_out, and_2_out, and_3_out, multiplexer_1_out, multiplexer_2_out;
  wire [2:0] multiplexer_3_out, multiplexer_4_out, multiplexer_5_out, multiplexer_6_out, multiplexer_7_out,
       multiplexer_8_out;
  wire [3:0] subtractor_1_out, subtractor_2_out;
  wire [7:0] not_1_out, shifter_1_out, shifter_2_out, shifter_3_out, shifter_4_out, shifter_5_out,
       shifter_5_out_2;
  wire [15:0] shifter_6_out;

  Subtractor #(.width(4)) subtractor_1 (
    .a(4'b1000), .b({1'b0, addr_unused}), .out(subtractor_1_out));  // open: bin, bout
  Subtractor #(.width(4)) subtractor_2 (.a(4'b1000), .b({1'b0, addr_used}), .out(subtractor_2_out));  // open: bin, bout
  Shifter shifter_1 (.in(instr_buffer_stat_reg), .\dist (subtractor_2_out[2:0]), .out(shifter_1_out));
  Shifter #(.shift("lr")) shifter_2 (.in(instr_buffer_stat_reg), .\dist (addr_used), .out(shifter_2_out));
  Shifter shifter_3 (.in(shifter_5_out_2), .\dist (subtractor_1_out[2:0]), .out(shifter_3_out));
  Shifter #(.shift("lr")) shifter_4 (.in(shifter_5_out_2), .\dist (addr_unused), .out(shifter_4_out));
  Multiplexer #(.enable("false")) multiplexer_1 (.in0(pause), .in1(1'b0), .out(multiplexer_1_out), .sel(unset));
  Shifter #(.width(16)) shifter_5 (
    .in({shifter_2_out[7:1], 1'b1, shifter_1_out}), .\dist ({1'b0, addr_used}),
    .out({shifter_5_out_2, shifter_5_out}));
  Shifter #(.width(16)) shifter_6 (
    .in({shifter_4_out[7:1], 1'b0, shifter_3_out}), .\dist ({1'b0, addr_unused}), .out(shifter_6_out));
  Register #(.width(1)) register_1 (.D(and_1_out), .clk(clock), .Q(rm_delay), .clr(reset));  // open: en
  and and_1 (and_1_out, ~rm_delay, read_miss);  // AND_Gate
  Register #(.width(1)) register_2 (.D(and_2_out), .clk(clock), .Q(wm_delay), .clr(reset));  // open: en
  and and_2 (and_2_out, ~wm_delay, write_miss);  // AND_Gate
  Register #(.width(1)) register_3 (.D(and_3_out), .clk(clock), .Q(rh_delay), .clr(reset));  // open: en
  and and_3 (and_3_out, ~rh_delay, read_hit);  // AND_Gate
  Register #(.width(1)) register_4 (.D(multiplexer_2_out), .clk(clock), .Q(pause), .clr(reset));  // open: en
  Multiplexer #(.enable("false")) multiplexer_2 (
    .in0(multiplexer_1_out), .in1(1'b1), .out(multiplexer_2_out), .sel(set));
  Register register_5 (.D(shifter_6_out[15:8]), .en(enable), .clk(clock), .Q(instr_buffer_stat_reg), .clr(reset));
  assign not_1_out = ~instr_buffer_stat_reg;  // NOT_Gate not_1, 8 bits wide
  Multiplexer #(.width(3), .enable("false")) multiplexer_3 (
    .in0(3'b000), .in1(3'b111), .out(multiplexer_3_out), .sel(not_1_out[7]));
  Multiplexer #(.width(3), .enable("false")) multiplexer_4 (
    .in0(multiplexer_3_out), .in1(3'b110), .out(multiplexer_4_out), .sel(not_1_out[6]));
  Multiplexer #(.width(3), .enable("false")) multiplexer_5 (
    .in0(multiplexer_4_out), .in1(3'b101), .out(multiplexer_5_out), .sel(not_1_out[5]));
  Multiplexer #(.width(3), .enable("false")) multiplexer_6 (
    .in0(multiplexer_5_out), .in1(3'b100), .out(multiplexer_6_out), .sel(not_1_out[4]));
  Multiplexer #(.width(3), .enable("false")) multiplexer_7 (
    .in0(multiplexer_6_out), .in1(3'b011), .out(multiplexer_7_out), .sel(not_1_out[3]));
  Multiplexer #(.width(3), .enable("false")) multiplexer_8 (
    .in0(multiplexer_7_out), .in1(3'b010), .out(multiplexer_8_out), .sel(not_1_out[2]));
  Multiplexer #(.width(3), .enable("false")) multiplexer_9 (
    .in0(multiplexer_8_out), .in1(3'b001), .out(free_addr), .sel(not_1_out[1]));
endmodule

module RAT_write (
  input  [2:0] rd,
  input  [2:0] rs1,
  input  [2:0] rs2,
  input  [2:0] rd_check,
  input  enable,
  input  reset,
  input  clock,
  output [2:0] rs1_count,
  output [2:0] rs2_count
);

  wire and_1_out, and_2_out, and_3_out, and_4_out, and_5_out, and_6_out, and_7_out, and_8_out, and_9_out,
       and_10_out, and_11_out, and_12_out, and_13_out, and_14_out, comparator_1_eq, comparator_2_eq,
       comparator_3_eq, comparator_4_eq, comparator_5_eq, comparator_6_eq, comparator_7_eq, comparator_8_eq,
       comparator_9_eq, comparator_10_eq, comparator_11_eq, comparator_12_eq, comparator_13_eq,
       comparator_14_eq, or_1_out, or_2_out, or_3_out, or_4_out, or_5_out, or_6_out, or_7_out;
  wire [2:0] adder_1_out, adder_2_out, adder_3_out, adder_4_out, adder_5_out, adder_6_out, adder_7_out,
       multiplexer_1_out, multiplexer_2_out, multiplexer_3_out, multiplexer_4_out, multiplexer_5_out,
       multiplexer_6_out, multiplexer_7_out, multiplexer_8_out, multiplexer_9_out, multiplexer_10_out,
       multiplexer_11_out, multiplexer_12_out, multiplexer_13_out, multiplexer_14_out, register_1_q,
       register_2_q, register_3_q, register_4_q, register_5_q, register_6_q, register_7_q, subtractor_1_out,
       subtractor_2_out, subtractor_3_out, subtractor_4_out, subtractor_5_out, subtractor_6_out,
       subtractor_7_out;

  Comparator #(.width(3), .mode("unsigned")) comparator_1 (.a(rd), .b(3'b001), .eq(comparator_1_eq));  // open: gt, lt
  Comparator #(.width(3), .mode("unsigned")) comparator_2 (
    .a(rd_check), .b(3'b001), .eq(comparator_2_eq));  // open: gt, lt
  Comparator #(.width(3), .mode("unsigned")) comparator_3 (.a(rd), .b(3'b010), .eq(comparator_3_eq));  // open: gt, lt
  Comparator #(.width(3), .mode("unsigned")) comparator_4 (
    .a(rd_check), .b(3'b010), .eq(comparator_4_eq));  // open: gt, lt
  Comparator #(.width(3), .mode("unsigned")) comparator_5 (.a(rd), .b(3'b011), .eq(comparator_5_eq));  // open: gt, lt
  Comparator #(.width(3), .mode("unsigned")) comparator_6 (
    .a(rd_check), .b(3'b011), .eq(comparator_6_eq));  // open: gt, lt
  Comparator #(.width(3), .mode("unsigned")) comparator_7 (.a(rd), .b(3'b100), .eq(comparator_7_eq));  // open: gt, lt
  Comparator #(.width(3), .mode("unsigned")) comparator_8 (
    .a(rd_check), .b(3'b100), .eq(comparator_8_eq));  // open: gt, lt
  Comparator #(.width(3), .mode("unsigned")) comparator_9 (.a(rd), .b(3'b101), .eq(comparator_9_eq));  // open: gt, lt
  Comparator #(.width(3), .mode("unsigned")) comparator_10 (
    .a(rd_check), .b(3'b101), .eq(comparator_10_eq));  // open: gt, lt
  Comparator #(.width(3), .mode("unsigned")) comparator_11 (.a(rd), .b(3'b110), .eq(comparator_11_eq));  // open: gt, lt
  Comparator #(.width(3), .mode("unsigned")) comparator_12 (
    .a(rd_check), .b(3'b110), .eq(comparator_12_eq));  // open: gt, lt
  Comparator #(.width(3), .mode("unsigned")) comparator_13 (.a(rd), .b(3'b111), .eq(comparator_13_eq));  // open: gt, lt
  Comparator #(.width(3), .mode("unsigned")) comparator_14 (
    .a(rd_check), .b(3'b111), .eq(comparator_14_eq));  // open: gt, lt
  or or_1 (or_1_out, comparator_1_eq, comparator_2_eq);
  or or_2 (or_2_out, comparator_3_eq, comparator_4_eq);
  or or_3 (or_3_out, comparator_5_eq, comparator_6_eq);
  or or_4 (or_4_out, comparator_7_eq, comparator_8_eq);
  or or_5 (or_5_out, comparator_9_eq, comparator_10_eq);
  or or_6 (or_6_out, comparator_11_eq, comparator_12_eq);
  or or_7 (or_7_out, comparator_13_eq, comparator_14_eq);
  and and_1 (and_1_out, or_1_out, enable);
  and and_2 (and_2_out, or_2_out, enable);
  and and_3 (and_3_out, or_3_out, enable);
  and and_4 (and_4_out, or_4_out, enable);
  and and_5 (and_5_out, or_5_out, enable);
  and and_6 (and_6_out, or_6_out, enable);
  and and_7 (and_7_out, or_7_out, enable);
  Adder #(.width(3)) adder_1 (.a(register_1_q), .b(3'b001), .out(adder_1_out));  // open: cin, cout
  Multiplexer #(.width(3), .enable("false")) multiplexer_1 (
    .in0(adder_1_out), .in1(subtractor_1_out), .out(multiplexer_1_out), .sel(comparator_2_eq));
  Subtractor #(.width(3)) subtractor_1 (.a(register_1_q), .b(3'b001), .out(subtractor_1_out));  // open: bin, bout
  Adder #(.width(3)) adder_2 (.a(register_2_q), .b(3'b001), .out(adder_2_out));  // open: cin, cout
  Multiplexer #(.width(3), .enable("false")) multiplexer_2 (
    .in0(adder_2_out), .in1(subtractor_2_out), .out(multiplexer_2_out), .sel(comparator_4_eq));
  Subtractor #(.width(3)) subtractor_2 (.a(register_2_q), .b(3'b001), .out(subtractor_2_out));  // open: bin, bout
  Adder #(.width(3)) adder_3 (.a(register_3_q), .b(3'b001), .out(adder_3_out));  // open: cin, cout
  Multiplexer #(.width(3), .enable("false")) multiplexer_3 (
    .in0(adder_3_out), .in1(subtractor_3_out), .out(multiplexer_3_out), .sel(comparator_6_eq));
  Subtractor #(.width(3)) subtractor_3 (.a(register_3_q), .b(3'b001), .out(subtractor_3_out));  // open: bin, bout
  Adder #(.width(3)) adder_4 (.a(register_4_q), .b(3'b001), .out(adder_4_out));  // open: cin, cout
  Subtractor #(.width(3)) subtractor_4 (.a(register_4_q), .b(3'b001), .out(subtractor_4_out));  // open: bin, bout
  Adder #(.width(3)) adder_5 (.a(register_5_q), .b(3'b001), .out(adder_5_out));  // open: cin, cout
  Subtractor #(.width(3)) subtractor_5 (.a(register_5_q), .b(3'b001), .out(subtractor_5_out));  // open: bin, bout
  Adder #(.width(3)) adder_6 (.a(register_6_q), .b(3'b001), .out(adder_6_out));  // open: cin, cout
  Subtractor #(.width(3)) subtractor_6 (.a(register_6_q), .b(3'b001), .out(subtractor_6_out));  // open: bin, bout
  Adder #(.width(3)) adder_7 (.a(register_7_q), .b(3'b001), .out(adder_7_out));  // open: cin, cout
  Subtractor #(.width(3)) subtractor_7 (.a(register_7_q), .b(3'b001), .out(subtractor_7_out));  // open: bin, bout
  Multiplexer #(.width(3), .enable("false")) multiplexer_4 (
    .in0(multiplexer_1_out), .in1(register_1_q), .out(multiplexer_4_out), .sel(and_8_out));
  and and_8 (and_8_out, comparator_2_eq, comparator_1_eq);
  Multiplexer #(.width(3), .enable("false")) multiplexer_5 (
    .in0(multiplexer_2_out), .in1(register_2_q), .out(multiplexer_5_out), .sel(and_9_out));
  and and_9 (and_9_out, comparator_4_eq, comparator_3_eq);
  Multiplexer #(.width(3), .enable("false")) multiplexer_6 (
    .in0(multiplexer_3_out), .in1(register_3_q), .out(multiplexer_6_out), .sel(and_10_out));
  and and_10 (and_10_out, comparator_6_eq, comparator_5_eq);
  Multiplexer #(.width(3), .enable("false")) multiplexer_7 (
    .in0(adder_4_out), .in1(subtractor_4_out), .out(multiplexer_7_out), .sel(comparator_8_eq));
  Multiplexer #(.width(3), .enable("false")) multiplexer_8 (
    .in0(multiplexer_7_out), .in1(register_4_q), .out(multiplexer_8_out), .sel(and_11_out));
  and and_11 (and_11_out, comparator_8_eq, comparator_7_eq);
  Multiplexer #(.width(3), .enable("false")) multiplexer_9 (
    .in0(adder_5_out), .in1(subtractor_5_out), .out(multiplexer_9_out), .sel(comparator_10_eq));
  Multiplexer #(.width(3), .enable("false")) multiplexer_10 (
    .in0(multiplexer_9_out), .in1(register_5_q), .out(multiplexer_10_out), .sel(and_12_out));
  and and_12 (and_12_out, comparator_10_eq, comparator_9_eq);
  Multiplexer #(.width(3), .enable("false")) multiplexer_11 (
    .in0(adder_6_out), .in1(subtractor_6_out), .out(multiplexer_11_out), .sel(comparator_12_eq));
  Multiplexer #(.width(3), .enable("false")) multiplexer_12 (
    .in0(multiplexer_11_out), .in1(register_6_q), .out(multiplexer_12_out), .sel(and_13_out));
  and and_13 (and_13_out, comparator_12_eq, comparator_11_eq);
  Multiplexer #(.width(3), .enable("false")) multiplexer_13 (
    .in0(adder_7_out), .in1(subtractor_7_out), .out(multiplexer_13_out), .sel(comparator_14_eq));
  Multiplexer #(.width(3), .enable("false")) multiplexer_14 (
    .in0(multiplexer_13_out), .in1(register_7_q), .out(multiplexer_14_out), .sel(and_14_out));
  and and_14 (and_14_out, comparator_14_eq, comparator_13_eq);
  Register #(.width(3)) register_1 (.D(multiplexer_4_out), .en(and_1_out), .clk(clock), .Q(register_1_q), .clr(reset));
  Register #(.width(3)) register_2 (.D(multiplexer_5_out), .en(and_2_out), .clk(clock), .Q(register_2_q), .clr(reset));
  Register #(.width(3)) register_3 (.D(multiplexer_6_out), .en(and_3_out), .clk(clock), .Q(register_3_q), .clr(reset));
  Register #(.width(3)) register_4 (.D(multiplexer_8_out), .en(and_4_out), .clk(clock), .Q(register_4_q), .clr(reset));
  Register #(.width(3)) register_5 (.D(multiplexer_10_out), .en(and_5_out), .clk(clock), .Q(register_5_q), .clr(reset));
  Register #(.width(3)) register_6 (.D(multiplexer_12_out), .en(and_6_out), .clk(clock), .Q(register_6_q), .clr(reset));
  Register #(.width(3)) register_7 (.D(multiplexer_14_out), .en(and_7_out), .clk(clock), .Q(register_7_q), .clr(reset));
  Multiplexer #(.select(3), .width(3), .enable("false")) multiplexer_15 (
    .in0(3'b000), .in1(register_1_q), .in2(register_2_q), .in3(register_3_q), .in4(register_4_q),
    .in5(register_5_q), .in6(register_6_q), .in7(register_7_q), .out(rs1_count), .sel(rs1));
  Multiplexer #(.select(3), .width(3), .enable("false")) multiplexer_16 (
    .in0(3'b000), .in1(register_1_q), .in2(register_2_q), .in3(register_3_q), .in4(register_4_q),
    .in5(register_5_q), .in6(register_6_q), .in7(register_7_q), .out(rs2_count), .sel(rs2));
endmodule
module RAT_read (
  input  [2:0] rs1,
  input  [2:0] rs2,
  input  [2:0] rd,
  input  [2:0] rs1_check,
  input  [2:0] rs2_check,
  input  enable,
  input  reset,
  input  clock,
  output [2:0] rd_count
);

  wire and_1_out, and_2_out, and_3_out, and_4_out, and_5_out, and_6_out, and_7_out, and_8_out, and_9_out,
       and_10_out, and_11_out, and_12_out, and_13_out, and_14_out, comparator_1_eq, comparator_2_eq,
       comparator_3_eq, comparator_4_eq, comparator_5_eq, comparator_6_eq, comparator_7_eq, comparator_8_eq,
       comparator_9_eq, comparator_10_eq, comparator_11_eq, comparator_12_eq, comparator_13_eq,
       comparator_14_eq, comparator_15_eq, comparator_16_eq, comparator_17_eq, comparator_18_eq,
       comparator_19_eq, comparator_20_eq, comparator_21_eq, comparator_22_eq, comparator_23_eq,
       comparator_24_eq, comparator_25_eq, comparator_26_eq, comparator_27_eq, comparator_28_eq, or_1_out,
       or_2_out, or_3_out, or_4_out, or_5_out, or_6_out, or_7_out, or_8_out, or_9_out, or_10_out, or_11_out,
       or_12_out, or_13_out, or_14_out, or_15_out, or_16_out, or_17_out, or_18_out, or_19_out, or_20_out,
       or_21_out;
  wire [2:0] adder_1_out, adder_2_out, adder_3_out, adder_4_out, adder_5_out, adder_6_out, adder_7_out,
       multiplexer_1_out, multiplexer_2_out, multiplexer_3_out, multiplexer_4_out, multiplexer_5_out,
       multiplexer_6_out, multiplexer_7_out, multiplexer_8_out, multiplexer_9_out, multiplexer_10_out,
       multiplexer_11_out, multiplexer_12_out, multiplexer_13_out, multiplexer_14_out, register_1_q,
       register_2_q, register_3_q, register_4_q, register_5_q, register_6_q, register_7_q, subtractor_1_out,
       subtractor_2_out, subtractor_3_out, subtractor_4_out, subtractor_5_out, subtractor_6_out,
       subtractor_7_out;

  Comparator #(.width(3), .mode("unsigned")) comparator_1 (.a(rs1), .b(3'b001), .eq(comparator_1_eq));  // open: gt, lt
  Comparator #(.width(3), .mode("unsigned")) comparator_2 (.a(rs2), .b(3'b001), .eq(comparator_2_eq));  // open: gt, lt
  Comparator #(.width(3), .mode("unsigned")) comparator_3 (
    .a(rs1_check), .b(3'b001), .eq(comparator_3_eq));  // open: gt, lt
  Comparator #(.width(3), .mode("unsigned")) comparator_4 (
    .a(rs2_check), .b(3'b001), .eq(comparator_4_eq));  // open: gt, lt
  Comparator #(.width(3), .mode("unsigned")) comparator_5 (.a(rs1), .b(3'b010), .eq(comparator_5_eq));  // open: gt, lt
  Comparator #(.width(3), .mode("unsigned")) comparator_6 (.a(rs2), .b(3'b010), .eq(comparator_6_eq));  // open: gt, lt
  Comparator #(.width(3), .mode("unsigned")) comparator_7 (
    .a(rs1_check), .b(3'b010), .eq(comparator_7_eq));  // open: gt, lt
  Comparator #(.width(3), .mode("unsigned")) comparator_8 (
    .a(rs2_check), .b(3'b010), .eq(comparator_8_eq));  // open: gt, lt
  Comparator #(.width(3), .mode("unsigned")) comparator_9 (.a(rs1), .b(3'b011), .eq(comparator_9_eq));  // open: gt, lt
  Comparator #(.width(3), .mode("unsigned")) comparator_10 (
    .a(rs2), .b(3'b011), .eq(comparator_10_eq));  // open: gt, lt
  Comparator #(.width(3), .mode("unsigned")) comparator_11 (
    .a(rs1_check), .b(3'b011), .eq(comparator_11_eq));  // open: gt, lt
  Comparator #(.width(3), .mode("unsigned")) comparator_12 (
    .a(rs2_check), .b(3'b011), .eq(comparator_12_eq));  // open: gt, lt
  Comparator #(.width(3), .mode("unsigned")) comparator_13 (
    .a(rs1), .b(3'b100), .eq(comparator_13_eq));  // open: gt, lt
  Comparator #(.width(3), .mode("unsigned")) comparator_14 (
    .a(rs2), .b(3'b100), .eq(comparator_14_eq));  // open: gt, lt
  Comparator #(.width(3), .mode("unsigned")) comparator_15 (
    .a(rs1_check), .b(3'b100), .eq(comparator_15_eq));  // open: gt, lt
  Comparator #(.width(3), .mode("unsigned")) comparator_16 (
    .a(rs2_check), .b(3'b100), .eq(comparator_16_eq));  // open: gt, lt
  Comparator #(.width(3), .mode("unsigned")) comparator_17 (
    .a(rs1), .b(3'b101), .eq(comparator_17_eq));  // open: gt, lt
  Comparator #(.width(3), .mode("unsigned")) comparator_18 (
    .a(rs2), .b(3'b101), .eq(comparator_18_eq));  // open: gt, lt
  Comparator #(.width(3), .mode("unsigned")) comparator_19 (
    .a(rs1_check), .b(3'b101), .eq(comparator_19_eq));  // open: gt, lt
  Comparator #(.width(3), .mode("unsigned")) comparator_20 (
    .a(rs2_check), .b(3'b101), .eq(comparator_20_eq));  // open: gt, lt
  Comparator #(.width(3), .mode("unsigned")) comparator_21 (
    .a(rs1), .b(3'b110), .eq(comparator_21_eq));  // open: gt, lt
  Comparator #(.width(3), .mode("unsigned")) comparator_22 (
    .a(rs2), .b(3'b110), .eq(comparator_22_eq));  // open: gt, lt
  Comparator #(.width(3), .mode("unsigned")) comparator_23 (
    .a(rs1_check), .b(3'b110), .eq(comparator_23_eq));  // open: gt, lt
  Comparator #(.width(3), .mode("unsigned")) comparator_24 (
    .a(rs2_check), .b(3'b110), .eq(comparator_24_eq));  // open: gt, lt
  Comparator #(.width(3), .mode("unsigned")) comparator_25 (
    .a(rs1), .b(3'b111), .eq(comparator_25_eq));  // open: gt, lt
  Comparator #(.width(3), .mode("unsigned")) comparator_26 (
    .a(rs2), .b(3'b111), .eq(comparator_26_eq));  // open: gt, lt
  Comparator #(.width(3), .mode("unsigned")) comparator_27 (
    .a(rs1_check), .b(3'b111), .eq(comparator_27_eq));  // open: gt, lt
  Comparator #(.width(3), .mode("unsigned")) comparator_28 (
    .a(rs2_check), .b(3'b111), .eq(comparator_28_eq));  // open: gt, lt
  or or_1 (or_1_out, comparator_1_eq, comparator_2_eq);
  or or_2 (or_2_out, comparator_3_eq, comparator_4_eq);
  or or_3 (or_3_out, comparator_5_eq, comparator_6_eq);
  or or_4 (or_4_out, comparator_7_eq, comparator_8_eq);
  or or_5 (or_5_out, comparator_9_eq, comparator_10_eq);
  or or_6 (or_6_out, comparator_11_eq, comparator_12_eq);
  or or_7 (or_7_out, comparator_13_eq, comparator_14_eq);
  or or_8 (or_8_out, comparator_15_eq, comparator_16_eq);
  or or_9 (or_9_out, comparator_17_eq, comparator_18_eq);
  or or_10 (or_10_out, comparator_19_eq, comparator_20_eq);
  or or_11 (or_11_out, comparator_21_eq, comparator_22_eq);
  or or_12 (or_12_out, comparator_23_eq, comparator_24_eq);
  or or_13 (or_13_out, comparator_25_eq, comparator_26_eq);
  or or_14 (or_14_out, comparator_27_eq, comparator_28_eq);
  or or_15 (or_15_out, or_1_out, or_2_out);
  and and_1 (and_1_out, or_15_out, enable);
  or or_16 (or_16_out, or_3_out, or_4_out);
  and and_2 (and_2_out, or_16_out, enable);
  or or_17 (or_17_out, or_5_out, or_6_out);
  and and_3 (and_3_out, or_17_out, enable);
  or or_18 (or_18_out, or_7_out, or_8_out);
  and and_4 (and_4_out, or_18_out, enable);
  or or_19 (or_19_out, or_9_out, or_10_out);
  and and_5 (and_5_out, or_19_out, enable);
  or or_20 (or_20_out, or_11_out, or_12_out);
  and and_6 (and_6_out, or_20_out, enable);
  or or_21 (or_21_out, or_13_out, or_14_out);
  and and_7 (and_7_out, or_21_out, enable);
  Adder #(.width(3)) adder_1 (.a(register_1_q), .b(3'b001), .out(adder_1_out));  // open: cin, cout
  Subtractor #(.width(3)) subtractor_1 (.a(register_1_q), .b(3'b001), .out(subtractor_1_out));  // open: bin, bout
  Adder #(.width(3)) adder_2 (.a(register_2_q), .b(3'b001), .out(adder_2_out));  // open: cin, cout
  Subtractor #(.width(3)) subtractor_2 (.a(register_2_q), .b(3'b001), .out(subtractor_2_out));  // open: bin, bout
  Adder #(.width(3)) adder_3 (.a(register_3_q), .b(3'b001), .out(adder_3_out));  // open: cin, cout
  Subtractor #(.width(3)) subtractor_3 (.a(register_3_q), .b(3'b001), .out(subtractor_3_out));  // open: bin, bout
  Adder #(.width(3)) adder_4 (.a(register_4_q), .b(3'b001), .out(adder_4_out));  // open: cin, cout
  Subtractor #(.width(3)) subtractor_4 (.a(register_4_q), .b(3'b001), .out(subtractor_4_out));  // open: bin, bout
  Adder #(.width(3)) adder_5 (.a(register_5_q), .b(3'b001), .out(adder_5_out));  // open: cin, cout
  Subtractor #(.width(3)) subtractor_5 (.a(register_5_q), .b(3'b001), .out(subtractor_5_out));  // open: bin, bout
  Adder #(.width(3)) adder_6 (.a(register_6_q), .b(3'b001), .out(adder_6_out));  // open: cin, cout
  Subtractor #(.width(3)) subtractor_6 (.a(register_6_q), .b(3'b001), .out(subtractor_6_out));  // open: bin, bout
  Adder #(.width(3)) adder_7 (.a(register_7_q), .b(3'b001), .out(adder_7_out));  // open: cin, cout
  Subtractor #(.width(3)) subtractor_7 (.a(register_7_q), .b(3'b001), .out(subtractor_7_out));  // open: bin, bout
  Multiplexer #(.width(3), .enable("false")) multiplexer_1 (
    .in0(adder_1_out), .in1(subtractor_1_out), .out(multiplexer_1_out), .sel(or_2_out));
  and and_8 (and_8_out, or_2_out, or_1_out);
  Multiplexer #(.width(3), .enable("false")) multiplexer_2 (
    .in0(adder_2_out), .in1(subtractor_2_out), .out(multiplexer_2_out), .sel(or_4_out));
  and and_9 (and_9_out, or_4_out, or_3_out);
  Multiplexer #(.width(3), .enable("false")) multiplexer_3 (
    .in0(adder_3_out), .in1(subtractor_3_out), .out(multiplexer_3_out), .sel(or_6_out));
  and and_10 (and_10_out, or_6_out, or_5_out);
  Multiplexer #(.width(3), .enable("false")) multiplexer_4 (
    .in0(adder_4_out), .in1(subtractor_4_out), .out(multiplexer_4_out), .sel(or_8_out));
  and and_11 (and_11_out, or_8_out, or_7_out);
  Multiplexer #(.width(3), .enable("false")) multiplexer_5 (
    .in0(adder_5_out), .in1(subtractor_5_out), .out(multiplexer_5_out), .sel(or_10_out));
  and and_12 (and_12_out, or_10_out, or_9_out);
  Multiplexer #(.width(3), .enable("false")) multiplexer_6 (
    .in0(adder_6_out), .in1(subtractor_6_out), .out(multiplexer_6_out), .sel(or_12_out));
  and and_13 (and_13_out, or_12_out, or_11_out);
  Multiplexer #(.width(3), .enable("false")) multiplexer_7 (
    .in0(adder_7_out), .in1(subtractor_7_out), .out(multiplexer_7_out), .sel(or_14_out));
  and and_14 (and_14_out, or_14_out, or_13_out);
  Register #(.width(3)) register_1 (.D(multiplexer_8_out), .en(and_1_out), .clk(clock), .Q(register_1_q), .clr(reset));
  Multiplexer #(.width(3), .enable("false")) multiplexer_8 (
    .in0(multiplexer_1_out), .in1(register_1_q), .out(multiplexer_8_out), .sel(and_8_out));
  Register #(.width(3)) register_2 (.D(multiplexer_9_out), .en(and_2_out), .clk(clock), .Q(register_2_q), .clr(reset));
  Multiplexer #(.width(3), .enable("false")) multiplexer_9 (
    .in0(multiplexer_2_out), .in1(register_2_q), .out(multiplexer_9_out), .sel(and_9_out));
  Register #(.width(3)) register_3 (.D(multiplexer_10_out), .en(and_3_out), .clk(clock), .Q(register_3_q), .clr(reset));
  Multiplexer #(.width(3), .enable("false")) multiplexer_10 (
    .in0(multiplexer_3_out), .in1(register_3_q), .out(multiplexer_10_out), .sel(and_10_out));
  Register #(.width(3)) register_4 (.D(multiplexer_11_out), .en(and_4_out), .clk(clock), .Q(register_4_q), .clr(reset));
  Multiplexer #(.width(3), .enable("false")) multiplexer_11 (
    .in0(multiplexer_4_out), .in1(register_4_q), .out(multiplexer_11_out), .sel(and_11_out));
  Register #(.width(3)) register_5 (.D(multiplexer_12_out), .en(and_5_out), .clk(clock), .Q(register_5_q), .clr(reset));
  Multiplexer #(.width(3), .enable("false")) multiplexer_12 (
    .in0(multiplexer_5_out), .in1(register_5_q), .out(multiplexer_12_out), .sel(and_12_out));
  Register #(.width(3)) register_6 (.D(multiplexer_13_out), .en(and_6_out), .clk(clock), .Q(register_6_q), .clr(reset));
  Multiplexer #(.width(3), .enable("false")) multiplexer_13 (
    .in0(multiplexer_6_out), .in1(register_6_q), .out(multiplexer_13_out), .sel(and_13_out));
  Register #(.width(3)) register_7 (.D(multiplexer_14_out), .en(and_7_out), .clk(clock), .Q(register_7_q), .clr(reset));
  Multiplexer #(.width(3), .enable("false")) multiplexer_14 (
    .in0(multiplexer_7_out), .in1(register_7_q), .out(multiplexer_14_out), .sel(and_14_out));
  Multiplexer #(.select(3), .width(3), .enable("false")) multiplexer_15 (
    .in0(3'b000), .in1(register_1_q), .in2(register_2_q), .in3(register_3_q), .in4(register_4_q),
    .in5(register_5_q), .in6(register_6_q), .in7(register_7_q), .out(rd_count), .sel(rd));
endmodule

module RS_counter (
  input  [3:0] sum,
  input  [2:0] addr,
  input  enable,
  input  [1:0] m1,
  input  [1:0] m2,
  input  [1:0] m3,
  input  [1:0] m4,
  input  [1:0] m5,
  input  [1:0] m6,
  input  [1:0] m7,
  input  [7:0] reg_status_bit,
  input  reset,
  input  clock,
  output [2:0] reg_out
);

  wire and_1_out, and_2_out, and_3_out, and_4_out, and_5_out, and_6_out, and_7_out, comparator_1_eq,
       comparator_2_eq, comparator_3_eq, comparator_4_eq, comparator_5_eq, comparator_6_eq, comparator_7_eq,
       comparator_8_eq, comparator_9_eq, comparator_10_eq, comparator_11_eq, comparator_12_eq,
       comparator_13_eq, comparator_14_eq;
  wire [2:0] multiplexer_15_out, multiplexer_16_out, multiplexer_17_out, multiplexer_18_out,
       multiplexer_19_out, multiplexer_20_out;
  wire [3:0] multiplexer_1_out, multiplexer_2_out, multiplexer_3_out, multiplexer_4_out, multiplexer_5_out,
       multiplexer_6_out, multiplexer_7_out, multiplexer_8_out, multiplexer_9_out, multiplexer_10_out,
       multiplexer_11_out, multiplexer_12_out, multiplexer_13_out, multiplexer_14_out, register_1_q,
       register_2_q, register_3_q, register_4_q, register_5_q, register_6_q, register_7_q, subtractor_1_out,
       subtractor_2_out, subtractor_3_out, subtractor_4_out, subtractor_5_out, subtractor_6_out,
       subtractor_7_out;

  Subtractor #(.width(4)) subtractor_1 (.a(register_1_q), .b({2'b00, m1}), .out(subtractor_1_out));  // open: bin, bout
  Subtractor #(.width(4)) subtractor_2 (.a(register_2_q), .b({2'b00, m2}), .out(subtractor_2_out));  // open: bin, bout
  Comparator #(.width(3)) comparator_1 (.a(addr), .b(3'b010), .eq(comparator_1_eq));  // open: gt, lt
  Subtractor #(.width(4)) subtractor_3 (.a(register_3_q), .b({2'b00, m3}), .out(subtractor_3_out));  // open: bin, bout
  Subtractor #(.width(4)) subtractor_4 (.a(register_4_q), .b({2'b00, m4}), .out(subtractor_4_out));  // open: bin, bout
  Comparator #(.width(3)) comparator_2 (.a(addr), .b(3'b100), .eq(comparator_2_eq));  // open: gt, lt
  Subtractor #(.width(4)) subtractor_5 (.a(register_5_q), .b({2'b00, m5}), .out(subtractor_5_out));  // open: bin, bout
  Comparator #(.width(3)) comparator_3 (.a(addr), .b(3'b101), .eq(comparator_3_eq));  // open: gt, lt
  Subtractor #(.width(4)) subtractor_6 (.a(register_6_q), .b({2'b00, m6}), .out(subtractor_6_out));  // open: bin, bout
  Comparator #(.width(3)) comparator_4 (.a(addr), .b(3'b110), .eq(comparator_4_eq));  // open: gt, lt
  Subtractor #(.width(4)) subtractor_7 (.a(register_7_q), .b({2'b00, m7}), .out(subtractor_7_out));  // open: bin, bout
  Comparator #(.width(3)) comparator_5 (.a(addr), .b(3'b111), .eq(comparator_5_eq));  // open: gt, lt
  Multiplexer #(.width(4), .enable("false")) multiplexer_1 (
    .in0(register_1_q), .in1(subtractor_1_out), .out(multiplexer_1_out), .sel(reg_status_bit[1]));
  Multiplexer #(.width(4), .enable("false")) multiplexer_2 (
    .in0(multiplexer_1_out), .in1(sum), .out(multiplexer_2_out), .sel(comparator_6_eq));
  Comparator #(.width(3)) comparator_6 (.a(addr), .b(3'b001), .eq(comparator_6_eq));  // open: gt, lt
  Multiplexer #(.width(4), .enable("false")) multiplexer_3 (
    .in0(register_2_q), .in1(subtractor_2_out), .out(multiplexer_3_out), .sel(reg_status_bit[2]));
  Multiplexer #(.width(4), .enable("false")) multiplexer_4 (
    .in0(multiplexer_3_out), .in1(sum), .out(multiplexer_4_out), .sel(comparator_1_eq));
  Multiplexer #(.width(4), .enable("false")) multiplexer_5 (
    .in0(register_3_q), .in1(subtractor_3_out), .out(multiplexer_5_out), .sel(reg_status_bit[3]));
  Multiplexer #(.width(4), .enable("false")) multiplexer_6 (
    .in0(multiplexer_5_out), .in1(sum), .out(multiplexer_6_out), .sel(comparator_7_eq));
  Comparator #(.width(3)) comparator_7 (.a(addr), .b(3'b011), .eq(comparator_7_eq));  // open: gt, lt
  Multiplexer #(.width(4), .enable("false")) multiplexer_7 (
    .in0(register_4_q), .in1(subtractor_4_out), .out(multiplexer_7_out), .sel(reg_status_bit[4]));
  Multiplexer #(.width(4), .enable("false")) multiplexer_8 (
    .in0(multiplexer_7_out), .in1(sum), .out(multiplexer_8_out), .sel(comparator_2_eq));
  Multiplexer #(.width(4), .enable("false")) multiplexer_9 (
    .in0(register_5_q), .in1(subtractor_5_out), .out(multiplexer_9_out), .sel(reg_status_bit[5]));
  Multiplexer #(.width(4), .enable("false")) multiplexer_10 (
    .in0(multiplexer_9_out), .in1(sum), .out(multiplexer_10_out), .sel(comparator_3_eq));
  Multiplexer #(.width(4), .enable("false")) multiplexer_11 (
    .in0(register_6_q), .in1(subtractor_6_out), .out(multiplexer_11_out), .sel(reg_status_bit[6]));
  Multiplexer #(.width(4), .enable("false")) multiplexer_12 (
    .in0(multiplexer_11_out), .in1(sum), .out(multiplexer_12_out), .sel(comparator_4_eq));
  Multiplexer #(.width(4), .enable("false")) multiplexer_13 (
    .in0(register_7_q), .in1(subtractor_7_out), .out(multiplexer_13_out), .sel(reg_status_bit[7]));
  Multiplexer #(.width(4), .enable("false")) multiplexer_14 (
    .in0(multiplexer_13_out), .in1(sum), .out(multiplexer_14_out), .sel(comparator_5_eq));
  Register #(.width(4)) register_1 (.D(multiplexer_2_out), .en(enable), .clk(clock), .Q(register_1_q), .clr(reset));
  Register #(.width(4)) register_2 (.D(multiplexer_4_out), .en(enable), .clk(clock), .Q(register_2_q), .clr(reset));
  Register #(.width(4)) register_3 (.D(multiplexer_6_out), .en(enable), .clk(clock), .Q(register_3_q), .clr(reset));
  Register #(.width(4)) register_4 (.D(multiplexer_8_out), .en(enable), .clk(clock), .Q(register_4_q), .clr(reset));
  Register #(.width(4)) register_5 (.D(multiplexer_10_out), .en(enable), .clk(clock), .Q(register_5_q), .clr(reset));
  Register #(.width(4)) register_6 (.D(multiplexer_12_out), .en(enable), .clk(clock), .Q(register_6_q), .clr(reset));
  Register #(.width(4)) register_7 (.D(multiplexer_14_out), .en(enable), .clk(clock), .Q(register_7_q), .clr(reset));
  Comparator #(.width(4)) comparator_8 (.a(register_1_q), .b(4'b0000), .eq(comparator_8_eq));  // open: gt, lt
  and and_1 (and_1_out, comparator_8_eq, reg_status_bit[1]);
  Comparator #(.width(4)) comparator_9 (.a(register_2_q), .b(4'b0000), .eq(comparator_9_eq));  // open: gt, lt
  Comparator #(.width(4)) comparator_10 (.a(register_3_q), .b(4'b0000), .eq(comparator_10_eq));  // open: gt, lt
  Comparator #(.width(4)) comparator_11 (.a(register_4_q), .b(4'b0000), .eq(comparator_11_eq));  // open: gt, lt
  Comparator #(.width(4)) comparator_12 (.a(register_5_q), .b(4'b0000), .eq(comparator_12_eq));  // open: gt, lt
  Comparator #(.width(4)) comparator_13 (.a(register_6_q), .b(4'b0000), .eq(comparator_13_eq));  // open: gt, lt
  Comparator #(.width(4)) comparator_14 (.a(register_7_q), .b(4'b0000), .eq(comparator_14_eq));  // open: gt, lt
  Multiplexer #(.width(3), .enable("false")) multiplexer_15 (
    .in0(3'b000), .in1(3'b001), .out(multiplexer_15_out), .sel(and_1_out));
  Multiplexer #(.width(3), .enable("false")) multiplexer_16 (
    .in0(multiplexer_15_out), .in1(3'b010), .out(multiplexer_16_out), .sel(and_2_out));
  and and_2 (and_2_out, comparator_9_eq, reg_status_bit[2]);
  Multiplexer #(.width(3), .enable("false")) multiplexer_17 (
    .in0(multiplexer_16_out), .in1(3'b011), .out(multiplexer_17_out), .sel(and_3_out));
  and and_3 (and_3_out, comparator_10_eq, reg_status_bit[3]);
  Multiplexer #(.width(3), .enable("false")) multiplexer_18 (
    .in0(multiplexer_17_out), .in1(3'b100), .out(multiplexer_18_out), .sel(and_4_out));
  and and_4 (and_4_out, comparator_11_eq, reg_status_bit[4]);
  Multiplexer #(.width(3), .enable("false")) multiplexer_19 (
    .in0(multiplexer_18_out), .in1(3'b101), .out(multiplexer_19_out), .sel(and_5_out));
  and and_5 (and_5_out, comparator_12_eq, reg_status_bit[5]);
  Multiplexer #(.width(3), .enable("false")) multiplexer_20 (
    .in0(multiplexer_19_out), .in1(3'b110), .out(multiplexer_20_out), .sel(and_6_out));
  and and_6 (and_6_out, comparator_13_eq, reg_status_bit[6]);
  Multiplexer #(.width(3), .enable("false")) multiplexer_21 (
    .in0(multiplexer_20_out), .in1(3'b111), .out(reg_out), .sel(and_7_out));
  and and_7 (and_7_out, comparator_14_eq, reg_status_bit[7]);
endmodule

module RS_read_register (
  input  [2:0] rs,
  input  [2:0] addr,
  input  en,
  input  [2:0] rd_check,
  input  reset,
  input  clock,
  output out_7,
  output out_8,
  output out_9,
  output out_10,
  output out_11,
  output out_12,
  output out_13
);

  wire and_1_out, and_2_out, and_3_out, and_4_out, and_5_out, and_6_out, and_7_out, comparator_1_eq,
       comparator_2_eq, comparator_3_eq, comparator_4_eq, comparator_5_eq, comparator_6_eq, comparator_7_eq,
       comparator_8_eq, comparator_9_eq, comparator_10_eq, comparator_11_eq, comparator_12_eq,
       comparator_13_eq, comparator_14_eq;
  wire [2:0] multiplexer_1_out, multiplexer_2_out, multiplexer_3_out, multiplexer_4_out, multiplexer_5_out,
       multiplexer_6_out, multiplexer_7_out, register_1_q, register_2_q, register_3_q, register_4_q,
       register_5_q, register_6_q, register_7_q;

  Comparator #(.width(3)) comparator_1 (.a(addr), .b(3'b001), .eq(comparator_1_eq));  // open: gt, lt
  Comparator #(.width(3)) comparator_2 (.a(addr), .b(3'b010), .eq(comparator_2_eq));  // open: gt, lt
  Comparator #(.width(3)) comparator_3 (.a(addr), .b(3'b011), .eq(comparator_3_eq));  // open: gt, lt
  Comparator #(.width(3)) comparator_4 (.a(addr), .b(3'b100), .eq(comparator_4_eq));  // open: gt, lt
  Comparator #(.width(3)) comparator_5 (.a(addr), .b(3'b101), .eq(comparator_5_eq));  // open: gt, lt
  Comparator #(.width(3)) comparator_6 (.a(addr), .b(3'b110), .eq(comparator_6_eq));  // open: gt, lt
  Comparator #(.width(3)) comparator_7 (.a(addr), .b(3'b111), .eq(comparator_7_eq));  // open: gt, lt
  Multiplexer #(.width(3), .enable("false")) multiplexer_1 (
    .in0(register_1_q), .in1(rs), .out(multiplexer_1_out), .sel(and_1_out));
  and and_1 (and_1_out, comparator_1_eq, en);
  Multiplexer #(.width(3), .enable("false")) multiplexer_2 (
    .in0(register_2_q), .in1(rs), .out(multiplexer_2_out), .sel(and_2_out));
  and and_2 (and_2_out, comparator_2_eq, en);
  Multiplexer #(.width(3), .enable("false")) multiplexer_3 (
    .in0(register_3_q), .in1(rs), .out(multiplexer_3_out), .sel(and_3_out));
  and and_3 (and_3_out, comparator_3_eq, en);
  Multiplexer #(.width(3), .enable("false")) multiplexer_4 (
    .in0(register_4_q), .in1(rs), .out(multiplexer_4_out), .sel(and_4_out));
  and and_4 (and_4_out, comparator_4_eq, en);
  Multiplexer #(.width(3), .enable("false")) multiplexer_5 (
    .in0(register_5_q), .in1(rs), .out(multiplexer_5_out), .sel(and_5_out));
  and and_5 (and_5_out, comparator_5_eq, en);
  Multiplexer #(.width(3), .enable("false")) multiplexer_6 (
    .in0(register_6_q), .in1(rs), .out(multiplexer_6_out), .sel(and_6_out));
  and and_6 (and_6_out, comparator_6_eq, en);
  Multiplexer #(.width(3), .enable("false")) multiplexer_7 (
    .in0(register_7_q), .in1(rs), .out(multiplexer_7_out), .sel(and_7_out));
  and and_7 (and_7_out, comparator_7_eq, en);
  Register #(.width(3)) register_1 (.D(multiplexer_1_out), .en(and_1_out), .clk(clock), .Q(register_1_q), .clr(reset));
  Register #(.width(3)) register_2 (.D(multiplexer_2_out), .en(and_2_out), .clk(clock), .Q(register_2_q), .clr(reset));
  Register #(.width(3)) register_3 (.D(multiplexer_3_out), .en(and_3_out), .clk(clock), .Q(register_3_q), .clr(reset));
  Register #(.width(3)) register_4 (.D(multiplexer_4_out), .en(and_4_out), .clk(clock), .Q(register_4_q), .clr(reset));
  Register #(.width(3)) register_5 (.D(multiplexer_5_out), .en(and_5_out), .clk(clock), .Q(register_5_q), .clr(reset));
  Register #(.width(3)) register_6 (.D(multiplexer_6_out), .en(and_6_out), .clk(clock), .Q(register_6_q), .clr(reset));
  Register #(.width(3)) register_7 (.D(multiplexer_7_out), .en(and_7_out), .clk(clock), .Q(register_7_q), .clr(reset));
  Comparator #(.width(3)) comparator_8 (.a(register_1_q), .b(rd_check), .eq(comparator_8_eq));  // open: gt, lt
  Comparator #(.width(3)) comparator_9 (.a(register_2_q), .b(rd_check), .eq(comparator_9_eq));  // open: gt, lt
  Comparator #(.width(3)) comparator_10 (.a(register_3_q), .b(rd_check), .eq(comparator_10_eq));  // open: gt, lt
  Comparator #(.width(3)) comparator_11 (.a(register_4_q), .b(rd_check), .eq(comparator_11_eq));  // open: gt, lt
  Comparator #(.width(3)) comparator_12 (.a(register_5_q), .b(rd_check), .eq(comparator_12_eq));  // open: gt, lt
  Comparator #(.width(3)) comparator_13 (.a(register_6_q), .b(rd_check), .eq(comparator_13_eq));  // open: gt, lt
  Comparator #(.width(3)) comparator_14 (.a(register_7_q), .b(rd_check), .eq(comparator_14_eq));  // open: gt, lt
  and and_8 (out_7, comparator_8_eq, en);
  and and_9 (out_8, comparator_9_eq, en);
  and and_10 (out_9, comparator_10_eq, en);
  and and_11 (out_10, comparator_11_eq, en);
  and and_12 (out_11, comparator_12_eq, en);
  and and_13 (out_12, comparator_13_eq, en);
  and and_14 (out_13, comparator_14_eq, en);
endmodule

module RS_write_reg (
  input  [2:0] rd,
  input  [2:0] addr,
  input  en,
  input  [2:0] rs1_check,
  input  [2:0] rs2_check,
  input  reset,
  input  clock,
  output out_8,
  output out_9,
  output out_10,
  output out_11,
  output out_12,
  output out_13,
  output out_14
);

  wire and_1_out, and_2_out, and_3_out, and_4_out, and_5_out, and_6_out, and_7_out, comparator_1_eq,
       comparator_2_eq, comparator_3_eq, comparator_4_eq, comparator_5_eq, comparator_6_eq, comparator_7_eq,
       comparator_8_eq, comparator_9_eq, comparator_10_eq, comparator_11_eq, comparator_12_eq,
       comparator_13_eq, comparator_14_eq, comparator_15_eq, comparator_16_eq, comparator_17_eq,
       comparator_18_eq, comparator_19_eq, comparator_20_eq, comparator_21_eq, or_1_out, or_2_out, or_3_out,
       or_4_out, or_5_out, or_6_out, or_7_out;
  wire [2:0] multiplexer_1_out, multiplexer_2_out, multiplexer_3_out, multiplexer_4_out, multiplexer_5_out,
       multiplexer_6_out, multiplexer_7_out, register_1_q, register_2_q, register_3_q, register_4_q,
       register_5_q, register_6_q, register_7_q;

  Comparator #(.width(3)) comparator_1 (.a(addr), .b(3'b001), .eq(comparator_1_eq));  // open: gt, lt
  Comparator #(.width(3)) comparator_2 (.a(addr), .b(3'b010), .eq(comparator_2_eq));  // open: gt, lt
  Comparator #(.width(3)) comparator_3 (.a(addr), .b(3'b011), .eq(comparator_3_eq));  // open: gt, lt
  Comparator #(.width(3)) comparator_4 (.a(addr), .b(3'b100), .eq(comparator_4_eq));  // open: gt, lt
  Comparator #(.width(3)) comparator_5 (.a(addr), .b(3'b101), .eq(comparator_5_eq));  // open: gt, lt
  Comparator #(.width(3)) comparator_6 (.a(addr), .b(3'b110), .eq(comparator_6_eq));  // open: gt, lt
  Comparator #(.width(3)) comparator_7 (.a(addr), .b(3'b111), .eq(comparator_7_eq));  // open: gt, lt
  Multiplexer #(.width(3), .enable("false")) multiplexer_1 (
    .in0(register_1_q), .in1(rd), .out(multiplexer_1_out), .sel(and_1_out));
  and and_1 (and_1_out, comparator_1_eq, en);
  Multiplexer #(.width(3), .enable("false")) multiplexer_2 (
    .in0(register_2_q), .in1(rd), .out(multiplexer_2_out), .sel(and_2_out));
  and and_2 (and_2_out, comparator_2_eq, en);
  Multiplexer #(.width(3), .enable("false")) multiplexer_3 (
    .in0(register_3_q), .in1(rd), .out(multiplexer_3_out), .sel(and_3_out));
  and and_3 (and_3_out, comparator_3_eq, en);
  Multiplexer #(.width(3), .enable("false")) multiplexer_4 (
    .in0(register_4_q), .in1(rd), .out(multiplexer_4_out), .sel(and_4_out));
  and and_4 (and_4_out, comparator_4_eq, en);
  Multiplexer #(.width(3), .enable("false")) multiplexer_5 (
    .in0(register_5_q), .in1(rd), .out(multiplexer_5_out), .sel(and_5_out));
  and and_5 (and_5_out, comparator_5_eq, en);
  Multiplexer #(.width(3), .enable("false")) multiplexer_6 (
    .in0(register_6_q), .in1(rd), .out(multiplexer_6_out), .sel(and_6_out));
  and and_6 (and_6_out, comparator_6_eq, en);
  Multiplexer #(.width(3), .enable("false")) multiplexer_7 (
    .in0(register_7_q), .in1(rd), .out(multiplexer_7_out), .sel(and_7_out));
  and and_7 (and_7_out, comparator_7_eq, en);
  Register #(.width(3)) register_1 (.D(multiplexer_1_out), .en(and_1_out), .clk(clock), .Q(register_1_q), .clr(reset));
  Register #(.width(3)) register_2 (.D(multiplexer_2_out), .en(and_2_out), .clk(clock), .Q(register_2_q), .clr(reset));
  Register #(.width(3)) register_3 (.D(multiplexer_3_out), .en(and_3_out), .clk(clock), .Q(register_3_q), .clr(reset));
  Register #(.width(3)) register_4 (.D(multiplexer_4_out), .en(and_4_out), .clk(clock), .Q(register_4_q), .clr(reset));
  Register #(.width(3)) register_5 (.D(multiplexer_5_out), .en(and_5_out), .clk(clock), .Q(register_5_q), .clr(reset));
  Register #(.width(3)) register_6 (.D(multiplexer_6_out), .en(and_6_out), .clk(clock), .Q(register_6_q), .clr(reset));
  Register #(.width(3)) register_7 (.D(multiplexer_7_out), .en(and_7_out), .clk(clock), .Q(register_7_q), .clr(reset));
  Comparator #(.width(3)) comparator_8 (.a(register_1_q), .b(rs2_check), .eq(comparator_8_eq));  // open: gt, lt
  Comparator #(.width(3)) comparator_9 (.a(register_1_q), .b(rs1_check), .eq(comparator_9_eq));  // open: gt, lt
  Comparator #(.width(3)) comparator_10 (.a(register_2_q), .b(rs2_check), .eq(comparator_10_eq));  // open: gt, lt
  Comparator #(.width(3)) comparator_11 (.a(rs1_check), .b(register_2_q), .eq(comparator_11_eq));  // open: gt, lt
  Comparator #(.width(3)) comparator_12 (.a(rs2_check), .b(register_3_q), .eq(comparator_12_eq));  // open: gt, lt
  Comparator #(.width(3)) comparator_13 (.a(rs1_check), .b(register_3_q), .eq(comparator_13_eq));  // open: gt, lt
  Comparator #(.width(3)) comparator_14 (.a(rs2_check), .b(register_4_q), .eq(comparator_14_eq));  // open: gt, lt
  Comparator #(.width(3)) comparator_15 (.a(rs1_check), .b(register_4_q), .eq(comparator_15_eq));  // open: gt, lt
  Comparator #(.width(3)) comparator_16 (.a(rs2_check), .b(register_5_q), .eq(comparator_16_eq));  // open: gt, lt
  Comparator #(.width(3)) comparator_17 (.a(rs1_check), .b(register_5_q), .eq(comparator_17_eq));  // open: gt, lt
  Comparator #(.width(3)) comparator_18 (.a(rs2_check), .b(register_6_q), .eq(comparator_18_eq));  // open: gt, lt
  Comparator #(.width(3)) comparator_19 (.a(rs1_check), .b(register_6_q), .eq(comparator_19_eq));  // open: gt, lt
  Comparator #(.width(3)) comparator_20 (.a(rs2_check), .b(register_7_q), .eq(comparator_20_eq));  // open: gt, lt
  Comparator #(.width(3)) comparator_21 (.a(register_7_q), .b(rs1_check), .eq(comparator_21_eq));  // open: gt, lt
  or or_1 (or_1_out, comparator_8_eq, comparator_9_eq);
  and and_8 (out_8, or_1_out, en);
  or or_2 (or_2_out, comparator_10_eq, comparator_11_eq);
  and and_9 (out_9, or_2_out, en);
  or or_3 (or_3_out, comparator_12_eq, comparator_13_eq);
  and and_10 (out_10, or_3_out, en);
  or or_4 (or_4_out, comparator_14_eq, comparator_15_eq);
  and and_11 (out_11, or_4_out, en);
  or or_5 (or_5_out, comparator_16_eq, comparator_17_eq);
  and and_12 (out_12, or_5_out, en);
  or or_6 (or_6_out, comparator_18_eq, comparator_19_eq);
  and and_13 (out_13, or_6_out, en);
  or or_7 (or_7_out, comparator_20_eq, comparator_21_eq);
  and and_14 (out_14, or_7_out, en);
endmodule
